// Digital circuit ALU-shift-step.dig as structural Verilog
module ALU_shift_step (
  input  CLK,
  input  nCLK,
  input  nRESET,
  input  nEN,
  output SH_LOADLEN,
  output nSH_OUTPUT,
  output SH_RESET
);

  wire _74hc4017_1_q3, _74hc4017_1_q4, d_ff_as_1_q, d_ff_as_2_nq, nand_1_out, not_1_out, switchdt_1_p3;

  not not_1 (not_1_out, CLK);
  // SwitchDT switchdt_1: pin names not known; wires that end beside it: not_1_out, nCLK, switchdt_1_p3
  D_FF_AS d_ff_as_1 (.Set(1'b0), .D(1'b1), .C(CLK), .Clr(~nRESET), .Q(d_ff_as_1_q));  // open: nQ
  D_FF_AS d_ff_as_2 (.Set(1'b0), .D(1'b1), .C(_74hc4017_1_q4), .Clr(~nRESET), .nQ(d_ff_as_2_nq));  // open: Q
  nand nand_1 (nand_1_out, d_ff_as_1_q, d_ff_as_2_nq);
  _74HC4017 _74hc4017_1 (
    .CLK(switchdt_1_p3), .nEN(nEN), .MR(nand_1_out), .Q0(SH_LOADLEN), .Q1(SH_RESET), .Q3(_74hc4017_1_q3),
    .Q4(_74hc4017_1_q4));  // open: Q2, Q5, Q6, Q7, Q8, Q9, nQ59
  not not_2 (nSH_OUTPUT, _74hc4017_1_q3);
endmodule

/* Test case:
~CLK CLK ~EN ~RESET  SH-LOADLEN ~{SH-OUTPUT} SH-RESET

1    0   1   0       1          1            0
0    1   1   0       1          1            0

1    0   1   1       1          1            0
0    1   0   1       1          1            0

1    0   0   1       0          1            1
0    1   1   1       0          1            1

1    0   1   1       0          1            1
0    1   1   1       0          1            1

1    0   1   1       0          1            1
0    1   0   1       0          1            1

1    0   0   1       0          1            0
0    1   0   1       0          1            0

1    0   0   1       0          0            0
0    1   0   1       0          0            0

1    0   0   1       1          1            0
0    1   1   1       1          1            0

1    0   1   1       1          1            0
0    1   1   1       1          1            0

1    0   1   1       1          1            0
0    1   0   1       1          1            0

1    0   0   1       1          1            0
0    1   1   1       1          1            0

1    0   1   1       1          1            0
0    1   1   1       1          1            0

1    0   1   1       1          1            0
0    1   1   1       1          1            0

1    0   1   1       1          1            0
0    1   1   1       1          1            0
*/
