// Digital circuit ALU.dig as structural Verilog
module ALU (
  input  CLK,
  input  nCLK,
  input  BUS_CLK,
  input  A,
  input  B,
  input  N,
  input  ALU_nRESET,
  input  ALU_AUX,
  input  [2:0] S,
  input  nSTEPDONE,
  output FLAG,
  output OUT,
  output [5:0] DLEN,
  output DSUM,
  output C
);

  wire _74hc4017_1_p4, _74hc4017_1_p5, _74hc4017_1_p6, AND, d_ff_1_q, d_ff_as_2_nq, demultiplexer_1_out_0,
       demultiplexer_1_out_1, EQUAL, LT, LTU, multiplexer_1_out, multiplexer_2_out, nC_OUT, nNEG_OUT,
       nor_1_out, not_1_out, not_2_out, OR, or_1_out, SHIFT, XOR;

  D_FF #(.Default(1)) d_ff_1 (.D(ALU_AUX), .C(CLK), .Q(d_ff_1_q));  // open: nQ
  or or_1 (or_1_out, nSTEPDONE, d_ff_1_q);
  nor nor_1 (nor_1_out, XOR, d_ff_as_2_nq);
  ALU_comb alu_comb_1 (
    .A(A), .B(B), .C(C), .N(N), .XOR(XOR), .OR(OR), .AND(AND), .SUM(DSUM), .nC(nC_OUT), .nNEG(nNEG_OUT));
  Demultiplexer #(.Default(1)) demultiplexer_1 (
    .sel(N), .in(ALU_nRESET), .out_0(demultiplexer_1_out_0), .out_1(demultiplexer_1_out_1));
  not not_1 (not_1_out, ALU_nRESET);
  // _74HC4017 _74hc4017_1: pin names not known; wires that end beside it: nCLK, or_1_out, not_1_out, _74hc4017_1_p4, _74hc4017_1_p5, _74hc4017_1_p6
  D_FF_AS d_ff_as_1 (
    .Set(~demultiplexer_1_out_0), .D(nC_OUT), .C(BUS_CLK), .Clr(~demultiplexer_1_out_1), .Q(LTU), .nQ(C));
  D_FF_AS d_ff_as_2 (.Set(~ALU_nRESET), .D(nor_1_out), .C(BUS_CLK), .Clr(1'b0), .Q(EQUAL), .nQ(d_ff_as_2_nq));
  D_FF_AS d_ff_as_3 (.Set(1'b0), .D(nNEG_OUT), .C(BUS_CLK), .Clr(~ALU_nRESET), .nQ(LT));  // open: Q
  not not_2 (not_2_out, _74hc4017_1_p6);
  ALU_shifter alu_shifter_1 (
    .BUS_CLK(BUS_CLK), .SH_IN(A), .SH_LENIN(DSUM), .nLA(S[0]), .SH_LOADLEN(_74hc4017_1_p4),
    .SH_nOUTPUT(not_2_out), .SH_RESET(_74hc4017_1_p5), .SH_OUT(SHIFT), .DLEN(DLEN));
  Multiplexer #(.Selector_Bits(2)) multiplexer_1 (
    .sel(S[1:0]), .in_0(DSUM), .in_1(OR), .in_2(XOR), .in_3(AND), .out(multiplexer_1_out));
  Multiplexer #(.Selector_Bits(2)) multiplexer_2 (
    .sel(S[1:0]), .in_0(LTU), .in_1(LT), .in_2(EQUAL), .in_3(1'b0), .out(multiplexer_2_out));
  D_FF_AS d_ff_as_4 (.Set(1'b0), .D(multiplexer_2_out), .C(ALU_AUX), .Clr(1'b0), .Q(FLAG));  // open: nQ
  Multiplexer multiplexer_3 (.sel(S[2]), .in_0(multiplexer_1_out), .in_1(SHIFT), .out(OUT));

  // Other names for the same wires on the sheet: SUM = DSUM
endmodule

/* Test case Binary Operators:
CLK S          A        B        N ALU-~RESET FLAG-LATCH SH-LOADLEN SH-~OUTPUT SH-RESET   OUT           FLAG DLEN DSUM

loop (rep,32)

let A = random(1<<32);
let B = random(1<<32);

let ADD = 0;
let OR  = 1;
let XOR = 2;
let AND = 3;

# A+B

0    (ADD)     0        0        0 1          0          0          1          0          X             X    X    X
1    (ADD)     0        0        0 0          0          0          1          0          X             X    X    X

loop (i,32)
0    (ADD)     (A>>i&1) (B>>i&1) 0 1          0          0          1          0          ((A+B)>>i&1)  X    X    X
1    (ADD)     (A>>i&1) (B>>i&1) 0 1          0          0          1          0          X             X    X    X
end loop

#A-B

0    (ADD)     0        0        1 1          0          0          1          0          X             X    X    X
1    (ADD)     0        0        1 0          0          0          1          0          X             X    X    X

loop (i,32)
0    (ADD)     (A>>i&1) (B>>i&1) 1 1          0          0          1          0          ((A-B)>>i&1)  X    X    X
1    (ADD)     (A>>i&1) (B>>i&1) 1 1          0          0          1          0          X             X    X    X
end loop

#A|B

0    (OR)      0        0        1 1          0          0          1          0          X             X    X    X
1    (OR)      0        0        1 0          0          0          1          0          X             X    X    X

loop (i,32)
0    (OR)      (A>>i&1) (B>>i&1) 1 1          0          0          1          0          ((A|B)>>i&1)  X    X    X
1    (OR)      (A>>i&1) (B>>i&1) 1 1          0          0          1          0          X             X    X    X
end loop


#A^B

0    (XOR)     0        0        1 1          0          0          1          0          X             X    X    X
1    (XOR)     0        0        1 0          0          0          1          0          X             X    X    X

loop (i,32)
0    (XOR)     (A>>i&1) (B>>i&1) 1 1          0          0          1          0          ((A^B)>>i&1)  X    X    X
1    (XOR)     (A>>i&1) (B>>i&1) 1 1          0          0          1          0          X             X    X    X
end loop


#A&B

0    (AND)     0        0        1 1          0          0          1          0          X             X    X    X
1    (AND)     0        0        1 0          0          0          1          0          X             X    X    X

loop (i,32)
0    (AND)     (A>>i&1) (B>>i&1) 1 1          0          0          1          0          ((A&B)>>i&1)  X    X    X
1    (AND)     (A>>i&1) (B>>i&1) 1 1          0          0          1          0          X             X    X    X
end loop

end loop
*/

/* Test case Flags:
CLK S          A        B        N ALU-~RESET FLAG-LATCH SH-LOADLEN SH-~OUTPUT SH-RESET   OUT           FLAG DLEN DSUM

loop (rep,32)

let LTU   = 0;
let LT    = 1;
let EQUAL = 2;

##############################################################################################################
#
# 0 <= A < B < (1<<31)

let A = random((1<<31)-1);
let B = A + 1 + random((1<<31)-2-A);
let U = 1;
let S = 1;
let E = 0;

# LTU

# Reset ALU

0    (LTU)     0        0        1 1          0          0          1          0          X             X    X    X
1    (LTU)     0        0        1 0          0          0          1          0          X             X    X    X

# Calculate

loop (i,32)
0    (LTU)     (A>>i&1) (B>>i&1) 1 1          0          0          1          0          X             X    X    X
1    (LTU)     (A>>i&1) (B>>i&1) 1 1          0          0          1          0          X             X    X    X
end loop

# Set and check flag

0    (LTU)     0        0        1 1          1          0          1          0          X             (U)  X    X
0    (LTU)     0        0        1 1          1          0          1          0          X             (U)  X    X
0    (LTU)     0        0        1 1          0          0          1          0          X             (U)  X    X
0    (LTU)     0        0        1 1          0          0          1          0          X             (U)  X    X
0    (LTU)     0        0        1 1          0          0          1          0          X             (U)  X    X

# LT

# Reset ALU

0    (LT)      0        0        1 1          0          0          1          0          X             X    X    X
1    (LT)      0        0        1 0          0          0          1          0          X             X    X    X

# Calculate

loop (i,32)
0    (LT)      (A>>i&1) (B>>i&1) 1 1          0          0          1          0          X             X    X    X
1    (LT)      (A>>i&1) (B>>i&1) 1 1          0          0          1          0          X             X    X    X
end loop

# Set and check flag

0    (LT)      0        0        1 1          1          0          1          0          X             (S)  X    X
1    (LT)      0        0        1 1          1          0          1          0          X             (S)  X    X
0    (LT)      0        0        1 1          0          0          1          0          X             (S)  X    X
1    (LT)      0        0        1 1          0          0          1          0          X             (S)  X    X
0    (LT)      0        0        1 1          0          0          1          0          X             (S)  X    X

# Equal

# Reset ALU

0    (EQUAL)   0        0        1 1          0          0          1          0          X             X    X    X
1    (EQUAL)   0        0        1 0          0          0          1          0          X             X    X    X

# Calculate

loop (i,32)
0    (EQUAL)   (A>>i&1) (B>>i&1) 1 1          0          0          1          0          X             X    X    X
1    (EQUAL)   (A>>i&1) (B>>i&1) 1 1          0          0          1          0          X             X    X    X
end loop

# Set and check flag 

0    (EQUAL)   0        0        1 1          1          0          1          0          X             (E)  X    X
1    (EQUAL)   0        0        1 1          1          0          1          0          X             (E)  X    X
0    (EQUAL)   0        0        1 1          0          0          1          0          X             (E)  X    X
1    (EQUAL)   0        0        1 1          0          0          1          0          X             (E)  X    X
0    (EQUAL)   0        0        1 1          0          0          1          0          X             (E)  X    X


##############################################################################################################
#
# 0 <= B < A < (1<<31)

let A = 1 + random((1<<31)-1);
let B = random(A);
let U = 0;
let S = 0;
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*/

/* Test case SLL/SRL:
CLK S          A         B        N ALU-~RESET FLAG-LATCH SH-LOADLEN SH-~OUTPUT SH-RESET   OUT           FLAG DLEN DSUM

let SLL = 6;

loop (rep,32)

let A = random(1<<32);
let B = random(32);

# SLL

let R = (A << B) & 0xFFFFFFFF;

# Reset ALU

0   (SLL)      0         0        0 1          0          0          1          0          X             X    X    X
0   (SLL)      0         0        0 0          0          0          1          0          X             X    X    X

# Load length

loop (i,32)
0   (SLL)      (31>>i&1) (B>>i&1) 0 1          0          1          1          0          X             X    X    X
1   (SLL)      (31>>i&1) (B>>i&1) 0 1          0          1          1          0          X             X    X    X
end loop

# Latch in length

0   (SLL)      0         0        0 1          0          0          1          1          X             X    X    X
0   (SLL)      0         0        0 1          0          0          1          1          X             X    X    X

# Load in argument

loop (i,32)
0   (SLL)      (A>>i&1)  0        0 1          0          0          1          0          X             X    X    X
1   (SLL)      (A>>i&1)  0        0 1          0          0          1          0          X             X    X    X
end loop

# Output result

loop (i,32)
0   (SLL)      0         0        0 1          0          0          0          0          (R>>i&1)      X    X    X
1   (SLL)      0         0        0 1          0          0          0          0          X             X    X    X
end loop

# SRL

let R = (A >> B) & 0xFFFFFFFF;

0   (SLL)      0         0        1 1          0          0          1          0          X             X    X    X
0   (SLL)      0         0        1 0          0          0          1          0          X             X    X    X

loop (i,32)
0   (SLL)      (31>>i&1) (B>>i&1) 1 1          0          1          1          0          X             X    X    X
1   (SLL)      (31>>i&1) (B>>i&1) 1 1          0          1          1          0          X             X    X    X
end loop

0   (SLL)      0         0        0 1          0          0          1          1          X             X    X    X
0   (SLL)      0         0        0 1          0          0          1          1          X             X    X    X

loop (i,32)
0   (SLL)      (A>>i&1)  0        0 1          0          0          1          0          X             X    X    X
1   (SLL)      (A>>i&1)  0        0 1          0          0          1          0          X             X    X    X
end loop

loop (i,32)
0   (SLL)      0         0        0 1          0          0          0          0          (R>>i&1)      X    X    X
1   (SLL)      0         0        0 1          0          0          0          0          X             X    X    X
end loop

end loop
*/

/* Test case SRA:
CLK S          A        B        N ALU-~RESET FLAG-LATCH  SH-LOADLEN SH-~OUTPUT SH-RESET   OUT           FLAG DLEN DSUM

loop (rep,4)

let SRA = 7;

# SRA

let A = random(1<<32);
let S = (A >> 31) & 1;

let B = 0;
let R = (A >> B) & 0xFFFFFFFF;

# Reset ALU

0   (SRA)      0         0        1 1          0          0          1          0          X             X    X    X
1   (SRA)      0         0        1 0          0          0          1          0          X             X    X    X

# Load shift length

loop (i,32)
0   (SRA)      (31>>i&1) (B>>i&1) 1 1          0          1          1          0          X             X    X    X
1   (SRA)      (31>>i&1) (B>>i&1) 1 1          0          1          1          0          X             X    X    X
end loop

# Latch length

0   (SRA)      0         0        1 1          0          0          1          1          X             X    X    X
1   (SRA)      0         0        1 1          0          0          1          1          X             X    X    X

# Load argument

loop (i,32)
0   (SRA)      (A>>i&1)  0        1 1          0          0          1          0          X             X    X    X
1   (SRA)      (A>>i&1)  0        1 1          0          0          1          0          X             X    X    X
end loop

# Output result

loop (i,32-0)
0   (SRA)      0         0        1 1          0          0          0          0          (R>>i&1)      X    X    X
1   (SRA)      0         0        1 1          0          0          0          0          X             X    X    X
end loop

loop (i,0)
0   (SRA)      0         0        1 1          0          0          0          0          (S)           X    X    X
1   (SRA)      0         0        1 1          0          0          0          0          X             X    X    X
end loop




let B = 1;
let R = (A >> B) & 0xFFFFFFFF;

0   (SRA)      0         0        1 1          0          0          1          0          X             X    X    X
1   (SRA)      0         0        1 0          0          0          1          0          X             X    X    X

loop (i,32)
0   (SRA)      (31>>i&1) (B>>i&1) 1 1          0          1          1          0          X             X    X    X
1   (SRA)      (31>>i&1) (B>>i&1) 1 1          0          1          1          0          X             X    X    X
end loop

0   (SRA)      0         0        1 1          0          0          1          1          X             X    X    X
1   (SRA)      0         0        1 1          0          0          1          1          X             X    X    X

loop (i,32)
0   (SRA)      (A>>i&1)  0        1 1          0          0          1          0          X             X    X    X
1   (SRA)      (A>>i&1)  0        1 1          0          0          1          0          X             X    X    X
end loop

loop (i,32-1)
0   (SRA)      0         0        1 1          0          0          0          0          (R>>i&1)      X    X    X
1   (SRA)      0         0        1 1          0          0          0          0          X             X    X    X
end loop

loop (i,1)
0   (SRA)      0         0        1 1          0          0          0          0          (S)           X    X    X
1   (SRA)      0         0        1 1          0          0          0          0          X             X    X    X
end loop



let B = 2;
let R = (A >> B) & 0xFFFFFFFF;

0   (SRA)      0         0        1 1          0          0          1          0          X             X    X    X
1   (SRA)      0         0        1 0          0          0          1          0          X             X    X    X

loop (i,32)
0   (SRA)      (31>>i&1) (B>>i&1) 1 1          0          1          1          0          X             X    X    X
1   (SRA)      (31>>i&1) (B>>i&1) 1 1          0          1          1          0          X             X    X    X
end loop

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*/
