// Digital circuit CPU.dig as structural Verilog
module CPU (
  input  CLK_RAW,
  input  [31:0] Breakpoint,
  output [31:0] x8_s0,
  output [31:0] x9_s1,
  output [31:0] x10_a0,
  output [31:0] PC,
  output [31:0] Address,
  output [31:0] Instr,
  output [7:0] Data_Read,
  output [5:0] Step,
  output [7:0] Substep,
  output [16:0] out_10,
  output [31:0] A,
  output [31:0] B,
  output [31:0] Result,
  output [11:0] CSR_Address,
  output [31:0] x11_a1,
  output [31:0] x4_tp,
  output [31:0] x5_t0,
  output [31:0] x6_t1,
  output [31:0] x7_t2,
  output [31:0] x1_ra,
  output [31:0] x2_sp,
  output [31:0] x3_gp,
  output [31:0] x12_a2,
  output [31:0] x13_a3,
  output [31:0] x14_a4,
  output [31:0] x15_a5,
  output [31:0] mepc,
  output [31:0] mscratch,
  output [31:0] mstatus,
  output [31:0] mie,
  output [31:0] mip,
  output [31:0] mcause,
  output [10:0] out_34,
  output [31:0] mtvec,
  output [7:0] Data_Write,
  output [31:0] Instr_2,
  output [31:0] Cycles,
  output [15:0] Instr16,
  output [7:0] out_41
);

  wire ADDR_CLK, ADDR_CLK_GATED, ADDR_IN, ADDR_LATCH, ALU_A, ALU_AUX, ALU_B, ALU_N, and_1_out, and_2_out,
       and_4_out, and_6_out, and_9_out, B_INSTR, B_RUN, B_STEP, B_STOP, B_SUBSTEP, BUS_CLK, BUS_EN,
       BUT_INSTR, BUT_STOP, button_1_out, button_2_out, CLK, clock_1_lastsubstep, CNT_2, comparator_1_eq,
       comparator_1_gt, comparator_1_lt, comparator_2_eq, CS_IO, CS_RAM, CS_ROM, CSR_ADDR_LATCH, CSR_IN,
       CSR_IN_LATCH, CSR_OUT, CSR_OUT_LATCH, CSR_PC_OUT, d_ff_2_q, d_ff_3_q, d_ff_as_1_q, d_ff_as_3_nq,
       d_ff_as_5_q, d_ff_as_6_nq, d_ff_as_7_q, d_ff_as_8_q, diodeforward_1_out, Imm, IMM_PC_OUT_SnP, ImmB,
       ImmCSR, ImmI, ImmJ, ImmS, ImmU, INT1P, INT2P, INT3P, LASTSTEP, LED_G, LED_R, Mem_Dval, MEM_IN,
       MEM_OUT, MEPC_OUT, mie_1_mei1e, mie_1_mei2e, mie_1_mei3e, MIE_t, mip_1_mei1p, mip_1_mei2p,
       mip_1_mei3p, MRET, MTVEC_OUT, multiplexer_1_out, multiplexer_8_out, nALU_RESET, nand_1_out, nCLK,
       nILL_OP, nILL_OP_FF, nIRQ, nKB_INT, nLEN4, nMEM_OE, nMEM_OE_OUT, nMEM_WE, nMEM_WE_OUT, nOPDONE,
       not_2_out, not_3_out, nREG_IN_EN, nRESET, nS_EXT, nSTEPDONE, nWAIT, nWAIT_t, nWAKEUP, nWAKEUP_t,
       OP_IMM_LATCH, OP_IN, OP_IN_MUX, OP_LATCH, OP_LATCH_LSB, opcode_1_p25, or_1_out, or_3_out, PC_CNT_EN,
       PC_IN, PC_IN_LATCH, PC_IN_MUX, PC_OUT, PC_OUT_LATCH, REG_IN, RESET, RS1, RSA, RSB, Running, SLEEP,
       SLEEP_t, Stopped, SUBSTEP_EN, SUBSTEP_EN_t, switch_1_a, switchdt_2_p4, TRAP_OP, TRAP_OP_SnP;
  wire [0:0] LEN;
  wire [1:0] ALU_A_MUX, REG_IN_MUX, TRAP2;
  wire [2:0] ALU_OP, IMM_MUX;
  wire [3:0] RSD;
  wire [7:0] DATA;
  wire [20:20] MicroCode_d;
  wire [31:0] DATA_ADDR;

  // RGBLED rgbled_1: pin names not known; wires that end beside it: LED_R, LED_G, 1'b0
  Comparator #(.Bits(32)) comparator_1 (
    .a(x3_gp), .b(32'h1), .gt(comparator_1_gt), .eq(comparator_1_eq), .lt(comparator_1_lt));
  and and_1 (and_1_out, nIRQ, nILL_OP_FF);
  D_FF #(.Default(1)) d_ff_1 (.D(nILL_OP), .C(CLK), .Q(nILL_OP_FF));  // open: nQ
  // RGBLED rgbled_2: pin names not known; wires that end beside it: comparator_1_gt, comparator_1_eq, comparator_1_lt
  Comparator #(.Bits(32)) comparator_2 (.a(Breakpoint), .b(PC), .eq(comparator_2_eq));  // open: gt, lt
  Button #(.activeLow("true")) Stop (.out(BUT_STOP));
  Button #(.activeLow("true")) Run (.out(B_RUN));
  Interrupt_Controller interrupt_controller_1 (
    .BUS_CLK(BUS_CLK), .IRQ_OP_SnP(TRAP_OP_SnP), .LASTSTEP(LASTSTEP), .nIRQ(and_1_out), .OP_LATCH(PC_CNT_EN),
    .nRESET(nRESET), .IRQ_OP(TRAP_OP), .IRQ_OP_FETCH(OP_IN_MUX));
  and and_2 (and_2_out, nRESET, nOPDONE);
  Switch switch_1 (.A(switch_1_a), .B(comparator_1_lt));
  D_FF d_ff_2 (.D(comparator_2_eq), .C(nOPDONE), .Q(d_ff_2_q));  // open: nQ
  PullUp pullup_1 (.out(switch_1_a));
  D_FF_AS #(.Default(1)) d_ff_as_1 (.Set(nCLK), .D(1'b0), .C(d_ff_2_q), .Clr(1'b0), .Q(d_ff_as_1_q));  // open: nQ
  D_FF_AS d_ff_as_2 (.Set(~1'b1), .D(1'b1), .C(ADDR_LATCH), .Clr(~and_2_out), .Q(TRAP_OP_SnP));  // open: nQ
  Button #(.activeLow("true")) One_Instruction (.out(BUT_INSTR));
  Button #(.activeLow("true")) One_Step (.out(B_STEP));
  Button #(.activeLow("true")) One_Substep (.out(B_SUBSTEP));
  D_FF #(.Default(1)) d_ff_3 (.D(switch_1_a), .C(~nOPDONE), .Q(d_ff_3_q));  // open: nQ
  DiodeBackward diodebackward_1 (.in(d_ff_3_q), .out(B_STOP));
  DiodeBackward diodebackward_2 (.in(BUT_STOP), .out(B_STOP));
  DiodeBackward diodebackward_3 (.in(d_ff_as_1_q), .out(B_INSTR));
  DiodeBackward diodebackward_4 (.in(BUT_INSTR), .out(B_INSTR));
  PullUp pullup_2 (.out(B_STOP));
  PullUp pullup_3 (.out(B_INSTR));
  Reset reset_1 (.out(nRESET));
  Reset #(.invertOutput("false")) reset_2 (.out(RESET));
  Multiplexer multiplexer_1 (.sel(ALU_A_MUX[0]), .in_0(RS1), .in_1(PC_OUT), .out(multiplexer_1_out));
  DebugShift32 debugshift32_1 (.CLK(BUS_CLK), .D(ALU_A), .nEN(1'b0), .Val(A));
  DebugShift32 debugshift32_2 (.CLK(BUS_CLK), .D(ALU_B), .nEN(1'b0), .Val(B));
  nand nand_1 (nand_1_out, OP_LATCH_LSB, CNT_2);
  // SwitchDT #(.poles(4)) switchdt_1: pin names not known; wires that end beside it: 1'b1, SUBSTEP_EN_t, nWAKEUP, 1'b1, SLEEP, 1'b0, nWAIT, 1'b1, SUBSTEP_EN, nWAKEUP_t, SLEEP_t, nWAIT_t
  Multiplexer multiplexer_2 (.sel(ALU_A_MUX[1]), .in_0(multiplexer_1_out), .in_1(ALU_A_MUX[0]), .out(ALU_A));
  // Mem mem_1: pin names not known; wires that end beside it: CLK, BUS_CLK, MEM_IN, ADDR_IN, ADDR_LATCH, ADDR_CLK_GATED, nMEM_OE, nMEM_WE, nS_EXT, nRESET, MEM_OUT, DATA, DATA_ADDR, Address, Mem_Dval, nMEM_OE_OUT
  D_FF #(.Bits(8)) d_ff_4 (.D(DATA), .C(nMEM_OE_OUT), .Q(Data_Read));  // open: nQ
  D_FF #(.Bits(8)) d_ff_5 (.D(DATA), .C(nMEM_WE_OUT), .Q(Data_Write));  // open: nQ
  Clock_driver clock_driver_1 (
    .CLK_RAW(CLK_RAW), .Stop(B_STOP), .Run(B_RUN), .One_Instruction(B_INSTR), .One_Step(B_STEP),
    .One_Substep(B_SUBSTEP), .STEPDONE(nSTEPDONE), .OPDONE(PC_CNT_EN), .RESET(nRESET), .WAKEUP(nWAKEUP_t),
    .nSLEEP(SLEEP_t), .nWAIT(nWAIT_t), .CLK(CLK), .CLK_2(nCLK), .nCLK(Running), .nCLK_2(Running),
    .LED_G(Stopped));  // open: LED_R
  nand nand_2 (nLEN4, LEN[0], BUS_EN);
  or or_1 (or_1_out, IMM_MUX[0], IMM_MUX[1], IMM_MUX[2]);
  DebugShift32 debugshift32_3 (.CLK(BUS_CLK), .D(ADDR_IN), .nEN(1'b0), .Val(Result));
  and and_3 (ADDR_CLK_GATED, ADDR_CLK, nand_1_out);
  Multiplexer multiplexer_3 (.sel(or_1_out), .in_0(MEM_IN), .in_1(Imm), .out(ALU_B));
  and and_4 (and_4_out, nWAKEUP, nRESET);
  not not_1 (Stopped, Running);
  or or_2 (LED_R, Stopped, ~SUBSTEP_EN_t);  // Or
  or or_3 (or_3_out, Running, ~SUBSTEP_EN_t);  // Or
  PullUp pullup_4 (.out(nWAIT));
  D_FF_AS d_ff_as_3 (.Set(1'b0), .D(1'b1), .C(SLEEP), .Clr(~and_4_out), .nQ(d_ff_as_3_nq));  // open: Q
  and and_5 (LED_G, or_3_out, ~Stopped);  // And
  nor nor_1 (LASTSTEP, LEN[0], BUS_EN);
  Clock clock_1 (
    .CLK(CLK), .nCLK(nCLK), .nLEN4(nLEN4), .LASTSTEP(LASTSTEP), .SUBSTEP_EN(SUBSTEP_EN), .nRESET(nRESET),
    .STEP(out_10[5:0]), .LASTSUBSTEP(clock_1_lastsubstep), .nSTEPDONE(nSTEPDONE), .SUBSTEP(Substep),
    .nOPDONE(nOPDONE));
  ALU alu_1 (
    .CLK(BUS_CLK), .A(ALU_A), .B(ALU_B), .N(ALU_N), .nRESET_ALU(nALU_RESET), .CLK_F(ALU_AUX), .S(ALU_OP),
    .FLAG(out_10[16]), .OUT(ADDR_IN));  // open: LOADLEN_SH, nOUTPUT_SH, RESET_SH, DLEN, DSUM, C
  // SwitchDT switchdt_2: pin names not known; wires that end beside it: nMEM_WE_OUT, nMEM_WE_OUT, 1'b1, switchdt_2_p4
  Terminal terminal_1 (
    .A(DATA_ADDR[15:0]), .nCS(CS_IO), .nWE(nMEM_WE_OUT), .nOE(nMEM_OE_OUT), .D(DATA), .nINT(nKB_INT));
  and and_6 (and_6_out, d_ff_as_3_nq, nWAIT);
  EEPROM #(.AddrBits(16), .Bits(8)) Firmware (
    .A(DATA_ADDR[15:0]), .CS(~CS_ROM), .WE(~switchdt_2_p4), .OE(~nMEM_OE_OUT), .D(DATA));
  RAMSinglePortSel #(.AddrBits(16), .Bits(8)) RAM (
    .A(DATA_ADDR[15:0]), .CS(~CS_RAM), .WE(~nMEM_WE_OUT), .OE(~nMEM_OE_OUT), .D(DATA));
  Demultiplexer #(.Selector_Bits(2), .Default(1)) demultiplexer_1 (
    .sel(DATA_ADDR[31:30]), .in(1'b0), .out_0(CS_ROM), .out_2(CS_RAM), .out_3(CS_IO));  // open: out_1
  and and_7 (BUS_CLK, CLK, BUS_EN);
  D_FF_AS d_ff_as_4 (.Set(~nRESET), .D(and_6_out), .C(CLK), .Clr(~and_6_out), .Q(SUBSTEP_EN_t));  // open: nQ
  Multiplexer multiplexer_4 (.sel(PC_IN_MUX), .in_0(ADDR_IN), .in_1(CSR_PC_OUT), .out(PC_IN));
  Multiplexer multiplexer_5 (.sel(OP_IN_MUX), .in_0(MEM_OUT), .in_1(TRAP_OP), .out(OP_IN));
  D_FF_AS d_ff_as_5 (.Set(~nRESET), .D(OP_LATCH), .C(CLK), .Clr(1'b0), .Q(d_ff_as_5_q));  // open: nQ
  Multiplexer #(.Selector_Bits(3)) multiplexer_6 (
    .sel(IMM_MUX), .in_0(ImmCSR), .in_1(ImmI), .in_2(ImmS), .in_3(ImmB), .in_4(ImmU), .in_5(ImmJ),
    .in_6(1'b0), .in_7(1'b1), .out(Imm));
  ROM #(.AddrBits(17), .isProgramMemory("true"), .Bits(32)) MicroCode (
    .A(out_10), .sel(1'b1),
    .D({REG_IN_MUX, IMM_MUX, ALU_A_MUX, PC_IN_MUX, CSR_IN_LATCH, CSR_OUT_LATCH, CSR_ADDR_LATCH, MicroCode_d[20], IMM_PC_OUT_SnP, OP_LATCH_LSB, nALU_RESET, ALU_AUX, ALU_OP, ALU_N, nREG_IN_EN, nMEM_WE, nMEM_OE, ADDR_CLK, ADDR_LATCH, nILL_OP, PC_OUT_LATCH, PC_IN_LATCH, OP_LATCH, SLEEP, BUS_EN, LEN[0]}));
  PC pc_1 (
    .CLK(CLK), .BUS_CLK(BUS_CLK), .IN(PC_IN), .LATCH_IN(PC_IN_LATCH), .LATCH_OUT(PC_OUT_LATCH),
    .SnP_OUT(IMM_PC_OUT_SnP), .nPE_CNT(PC_CNT_EN), .EN_CNT(CNT_2), .nRESET(nRESET), .OUT(PC_OUT), .PC(PC));
  D_FF_AS d_ff_as_6 (.Set(~nRESET), .D(d_ff_as_5_q), .C(nCLK), .Clr(1'b0), .nQ(d_ff_as_6_nq));  // open: Q
  // OpCode opcode_1: pin names not known; wires that end beside it: BUS_CLK, OP_IN, OP_LATCH, OP_LATCH_LSB, OP_IMM_LATCH, IMM_PC_OUT_SnP, nRESET, ImmI, ImmS, ImmB, ImmU, ImmJ, ImmCSR, RSA, RSB, RSD, out_10[10:6], out_10[13:11], out_10[15], nS_EXT, out_10[14], TRAP2, CNT_2, Instr, opcode_1_p25, Instr16, out_41
  and and_8 (PC_CNT_EN, OP_LATCH, d_ff_as_6_nq);
  D_FF d_ff_6 (.D(PC_CNT_EN), .C(CLK), .Q(OP_IMM_LATCH));  // open: nQ
  // Register_bank register_bank_1: pin names not known; wires that end beside it: BUS_CLK, REG_IN, nREG_IN_EN, RSA, RSB, RSD, RESET, RS1, MEM_IN
  Register_view register_view_1 (
    .BUS_CLK(BUS_CLK), .nREG_IN_EN(nREG_IN_EN), .REG_IN(REG_IN), .RSD(RSD), .x1_ra(x1_ra), .x2_sp(x2_sp),
    .x3_gp(x3_gp), .x4_tp(x4_tp), .x5_t0(x5_t0), .x6_t1(x6_t1), .x7_t2(x7_t2), .x8_s0_fp(x8_s0),
    .x9_s1(x9_s1), .x10_a0(x10_a0), .x11_a1(x11_a1), .x12_a2(x12_a2), .x13_a3(x13_a3), .x14_a4(x14_a4),
    .x15_a5(x15_a5));
  Multiplexer #(.Selector_Bits(2)) multiplexer_7 (
    .sel(REG_IN_MUX), .in_0(ADDR_IN), .in_1(MEM_OUT), .in_2(CSR_IN), .in_3(PC_OUT), .out(REG_IN));
  Button #(.activeLow("true")) button_1 (.out(button_1_out));
  Button #(.activeLow("true")) button_2 (.out(button_2_out));
  not not_2 (not_2_out, MRET);
  Multiplexer multiplexer_8 (.sel(out_10[13]), .in_0(RS1), .in_1(Imm), .out(multiplexer_8_out));
  PullDown pulldown_1 (.out(CSR_IN));
  and and_9 (and_9_out, not_2_out, PC_IN_MUX);
  D_FF_AS #(.Default(1)) d_ff_as_7 (.Set(CLK), .D(1'b0), .C(PC_IN_MUX), .Clr(1'b0), .Q(d_ff_as_7_q));  // open: nQ
  Counter #(.Bits(32)) counter_1 (.en(1'b1), .C(CLK), .clr(1'b0), .out(Cycles));  // open: ovf
  MIE mie_1 (
    .CLK(CLK), .BUS_CLK(BUS_CLK), .CSR_IN(CSR_OUT), .CSR_IN_LATCH(CSR_IN_LATCH),
    .CSR_OUT_LATCH(CSR_OUT_LATCH), .CSR_ADDR(CSR_Address), .nRESET(nRESET), .CSR_OUT(CSR_IN), .mie(mie),
    .MEI1E(mie_1_mei1e), .MEI2E(mie_1_mei2e), .MEI3E(mie_1_mei3e));
  MIP mip_1 (
    .CLK(CLK), .BUS_CLK(BUS_CLK), .CSR_IN(CSR_OUT), .CSR_IN_LATCH(CSR_IN_LATCH),
    .CSR_OUT_LATCH(CSR_OUT_LATCH), .CSR_ADDR(CSR_Address), .nINT1(nKB_INT), .nINT2(button_1_out),
    .nINT3(button_2_out), .nRESET(nRESET), .CSR_OUT(CSR_IN), .mip(mip), .MEI1P(mip_1_mei1p),
    .MEI2P(mip_1_mei2p), .MEI3P(mip_1_mei3p));
  MEPC mepc_1 (
    .BUS_CLK(BUS_CLK), .PC_IN(PC_OUT), .IN_EN(and_9_out), .CSR_IN(CSR_OUT), .CSR_IN_LATCH(CSR_IN_LATCH),
    .CSR_ADDR(CSR_Address), .RESET(RESET), .OUT(MEPC_OUT), .CSR_OUT(CSR_IN), .mepc(mepc));
  MSTATUS mstatus_1 (
    .CLK(CLK), .BUS_CLK(BUS_CLK), .CSR_IN(CSR_OUT), .CSR_IN_LATCH(CSR_IN_LATCH),
    .CSR_OUT_LATCH(CSR_OUT_LATCH), .CSR_ADDR(CSR_Address), .IRQ(PC_IN_MUX), .MRET(MRET),
    .IRQ_LATCH(d_ff_as_7_q), .RESET(RESET), .nRESET(nRESET), .CSR_OUT(CSR_IN), .mstatus(mstatus), .MIE(MIE_t));  // open: MPIE
  CSR csr_1 (
    .CLK(BUS_CLK), .INA(multiplexer_8_out), .INB(CSR_IN), .CSR_FUNC(out_10[12:11]), .ADDR_IN(Imm),
    .ADDR_LATCH(CSR_ADDR_LATCH), .nRESET(nRESET), .NEW_VAL(CSR_OUT), .ADDR(CSR_Address));
  Counter #(.Bits(32)) counter_2 (.en(1'b1), .C(~nOPDONE), .clr(1'b0), .out(Instr_2));  // open: ovf
  D_FF_AS #(.Default(1)) d_ff_as_8 (.Set(CLK), .D(MRET), .C(PC_IN_MUX), .Clr(1'b0), .Q(d_ff_as_8_q));  // open: nQ
  and and_10 (INT1P, mie_1_mei1e, mip_1_mei1p);
  and and_11 (INT2P, mie_1_mei2e, mip_1_mei2p);
  and and_12 (INT3P, mie_1_mei3e, mip_1_mei3p);
  not not_3 (not_3_out, TRAP2[0]);
  and and_13 (MRET, not_3_out, TRAP2[1]);
  MTVEC mtvec_1 (
    .BUS_CLK(BUS_CLK), .MTVEC_SnP(PC_IN_MUX), .CSR_IN(CSR_OUT), .CSR_IN_LATCH(CSR_IN_LATCH),
    .CSR_ADDR(CSR_Address), .RESET(RESET), .MTVEC_OUT(MTVEC_OUT), .CSR_OUT(CSR_IN), .mtvec(mtvec));
  MSCRATCH mscratch_1 (
    .BUS_CLK(BUS_CLK), .CSR_IN(CSR_OUT), .CSR_IN_LATCH(CSR_IN_LATCH), .CSR_ADDR(CSR_Address), .RESET(RESET),
    .CSR_OUT(CSR_IN), .mscratch(mscratch));
  MCAUSE mcause_1 (
    .BUS_CLK(BUS_CLK), .CSR_IN_LATCH(CSR_IN_LATCH), .CSR_OUT_LATCH(CSR_OUT_LATCH), .CSR_ADDR(CSR_Address),
    .TRAP2(TRAP2), .nIRQ(nIRQ), .INT1P(INT1P), .INT2P(INT2P), .INT3P(INT3P), .IRQ_LATCH(d_ff_as_8_q),
    .nRESET(nRESET), .CSR_OUT(CSR_IN), .mcause(mcause));
  DiodeForward diodeforward_1 (.in(INT1P), .out(diodeforward_1_out));
  DiodeForward diodeforward_2 (.in(INT2P), .out(diodeforward_1_out));
  DiodeForward diodeforward_3 (.in(INT3P), .out(diodeforward_1_out));
  Multiplexer multiplexer_9 (.sel(MRET), .in_0(MTVEC_OUT), .in_1(MEPC_OUT), .out(CSR_PC_OUT));
  PullDown pulldown_2 (.out(diodeforward_1_out));
  not not_4 (nWAKEUP, diodeforward_1_out);
  nand nand_3 (nIRQ, MIE_t, diodeforward_1_out);

  assign out_34 = out_10[16:6];
  assign Step = out_10[5:0];

  // Other names for the same wires on the sheet: LEN[1] = BUS_EN; IMM_SnP = IMM_PC_OUT_SnP;
  //   PC_OUT_SnP = IMM_PC_OUT_SnP; ALU_OUT = ADDR_IN; CntCycles[31:0] = Cycles; CntInstr[31:0] = Instr_2;
  //   CSR_ADDR[11:0] = CSR_Address; Da[31:0] = A; DATA_ADDR_16[15:0] = DATA_ADDR[15:0]; Db[31:0] = B;
  //   Dres[31:0] = Result; FLAG = out_10[16]; FUNC3[2:0] = out_10[13:11]; Mem_Addr[31:0] = Address;
  //   Mem_Data_R[7:0] = Data_Read; Mem_Data_W[7:0] = Data_Write; OPCODE[4:0] = out_10[10:6]; RS2 = MEM_IN;
  //   SA = out_10[15]; SYS = out_10[14]; x1[31:0] = x1_ra; x2[31:0] = x2_sp; x3[31:0] = x3_gp; x4[31:0] = x4_tp;
  //   x5[31:0] = x5_t0; x6[31:0] = x6_t1; x7[31:0] = x7_t2; x8[31:0] = x8_s0; x9[31:0] = x9_s1; x10[31:0] = x10_a0;
  //   x11[31:0] = x11_a1; x12[31:0] = x12_a2; x13[31:0] = x13_a3; x14[31:0] = x14_a4; x15[31:0] = x15_a5

  // Notes on the sheet:
  //   CLK_RAW: Hz: 20000
  //   Breakpoint: default 4294967295
  //   Debug
  //   Interrupts
  //   Clock
  //   ALU
  //   Memory
  //   contents of Firmware (hex, n*v repeats v):
  //   81,40,1,41,33,87,20,0,81,43,b7,4,2,0,89,4,5,4,63,4,77,0,6f,20,a0,54,85,40,5,41,33,
  //   87,20,0,89,43,b7,4,2,0,8d,4,5,4,63,4,77,0,6f,20,0,53,8d,40,1d,41,33,87,20,0,a9,43,
  //   b7,4,2,0,91,4,5,4,63,4,77,0,6f,20,60,51,81,40,37,81,ff,ff,33,87,20,0,e1,73,b7,4,2,
  //   0,95,4,5,4,63,4,77,0,6f,20,a0,4f,b7,0,0,80,1,41,33,87,20,0,b7,3,0,80,b7,4,2,0,99,
  //   4,5,4,63,4,77,0,6f,20,c0,4d,b7,0,0,80,37,81,ff,ff,33,87,20,0,b7,83,ff,7f,b7,4,2,0,
  //   9d,4,5,4,63,4,77,0,6f,20,c0,4b,81,40,37,81,0,0,7d,11,33,87,20,0,a1,63,fd,13,b7,4,
  //   2,0,a1,4,5,4,63,4,77,0,6f,20,c0,49,b7,0,0,80,fd,10,1,41,33,87,20,0,b7,3,0,80,fd,13,
  //   b7,4,2,0,a5,4,5,4,63,4,77,0,6f,20,a0,47,b7,0,0,80,fd,10,37,81,0,0,7d,11,33,87,20,
  //   0,b7,83,0,80,f9,13,b7,4,2,0,a9,4,5,4,63,4,77,0,6f,20,40,45,b7,0,0,80,37,81,0,0,7d,
  //   11,33,87,20,0,b7,83,0,80,fd,13,b7,4,2,0,ad,4,5,4,63,4,77,0,6f,20,0,43,b7,0,0,80,fd,
  //   10,37,81,ff,ff,33,87,20,0,b7,83,ff,7f,fd,13,b7,4,2,0,b1,4,5,4,63,4,77,0,6f,20,c0,
  //   40,81,40,13,1,f0,ff,33,87,20,0,93,3,f0,ff,b7,4,2,0,b5,4,5,4,63,4,77,0,6f,20,e0,3e,
  //   93,0,f0,ff,5,41,33,87,20,0,81,43,b7,4,2,0,b9,4,5,4,63,4,77,0,6f,20,20,3d,93,0,f0,
  //   ff,13,1,f0,ff,33,87,20,0,93,3,e0,ff,b7,4,2,0,bd,4,5,4,63,4,77,0,6f,20,20,3b,85,40,
  //   37,1,0,80,7d,11,33,87,20,0,b7,3,0,80,b7,4,2,0,c1,4,5,4,63,4,77,0,6f,20,20,39,b5,40,
  //   2d,41,8a,90,e1,43,b7,4,2,0,c5,4,5,4,63,84,70,0,6f,20,a0,37,b9,40,2d,41,6,91,e5,43,
  //   b7,4,2,0,c9,4,5,4,63,4,71,0,6f,20,20,36,b5,40,86,90,e9,43,b7,4,2,0,cd,4,5,4,63,84,
  //   70,0,6f,20,c0,34,1,42,b5,40,2d,41,33,87,20,0,13,3,7,0,5,2,89,42,e3,18,52,fe,e1,43,
  //   b7,4,2,0,d1,4,5,4,63,4,73,0,6f,20,40,32,1,42,b9,40,2d,41,33,87,20,0,1,0,13,3,7,0,
  //   5,2,89,42,e3,17,52,fe,e5,43,b7,4,2,0,d5,4,5,4,63,4,73,0,6f,20,a0,2f,1,42,bd,40,2d,
  //   41,33,87,20,0,1,0,1,0,13,3,7,0,5,2,89,42,e3,16,52,fe,e9,43,b7,4,2,0,d9,4,5,4,63,4,
  //   73,0,6f,20,e0,2c,1,42,b5,40,2d,41,33,87,20,0,5,2,89,42,e3,1a,52,fe,e1,43,b7,4,2,0,
  //   dd,4,5,4,63,4,77,0,6f,20,a0,2a,1,42,b9,40,2d,41,1,0,33,87,20,0,5,2,89,42,e3,19,52,
  //   fe,e5,43,b7,4,2,0,e1,4,5,4,63,4,77,0,6f,20,40,28,1,42,bd,40,2d,41,1,0,1,0,33,87,20,
  //   0,5,2,89,42,e3,18,52,fe,e9,43,b7,4,2,0,e5,4,5,4,63,4,77,0,6f,20,c0,25,1,42,b5,40,
  //   1,0,2d,41,33,87,20,0,5,2,89,42,e3,19,52,fe,e1,43,b7,4,2,0,e9,4,5,4,63,4,77,0,6f,20,
  //   60,23,1,42,b9,40,1,0,2d,41,1,0,33,87,20,0,5,2,89,42,e3,18,52,fe,e5,43,b7,4,2,0,ed,
  //   4,5,4,63,4,77,0,6f,20,e0,20,1,42,bd,40,1,0,1,0,2d,41,33,87,20,0,5,2,89,42,e3,18,52,
  //   fe,e9,43,b7,4,2,0,f1,4,5,4,63,4,77,0,6f,20,60,1e,1,42,2d,41,b5,40,33,87,20,0,5,2,
  //   89,42,e3,1a,52,fe,e1,43,b7,4,2,0,f5,4,5,4,63,4,77,0,6f,20,20,1c,1,42,2d,41,b9,40,
  //   1,0,33,87,20,0,5,2,89,42,e3,19,52,fe,e5,43,b7,4,2,0,f9,4,5,4,63,4,77,0,6f,20,c0,19,
  //   1,42,2d,41,bd,40,1,0,1,0,33,87,20,0,5,2,89,42,e3,18,52,fe,e9,43,b7,4,2,0,fd,4,5,4,
  //   63,4,77,0,6f,20,40,17,1,42,2d,41,1,0,b5,40,33,87,20,0,5,2,89,42,e3,19,52,fe,e1,43,
  //   b7,4,2,0,93,84,4,2,5,4,63,4,77,0,6f,20,c0,14,1,42,2d,41,1,0,b9,40,1,0,33,87,20,0,
  //   5,2,89,42,e3,18,52,fe,e5,43,b7,4,2,0,93,84,14,2,5,4,63,4,77,0,6f,20,20,12,1,42,2d,
  //   41,1,0,1,0,bd,40,33,87,20,0,5,2,89,42,e3,18,52,fe,e9,43,b7,4,2,0,93,84,24,2,5,4,63,
  //   4,77,0,6f,20,80,f,bd,40,33,1,10,0,bd,43,b7,4,2,0,93,84,34,2,5,4,63,4,71,0,6f,20,e0,
  //   d,93,0,0,2,33,81,0,0,93,3,0,2,b7,4,2,0,93,84,44,2,5,4,63,4,71,0,6f,20,0,c,b3,0,0,
  //   0,81,43,b7,4,2,0,93,84,54,2,5,4,63,84,70,0,6f,20,80,a,c1,40,79,41,33,80,20,0,81,43,
  //   b7,4,2,0,93,84,64,2,5,4,63,4,70,0,6f,20,c0,8,81,40,1,41,33,b7,20,0,81,43,b7,4,8,0,
  //   89,4,5,4,63,4,77,0,6f,20,20,7,85,40,5,41,33,b7,20,0,81,43,b7,4,8,0,8d,4,5,4,63,4,
  //   77,0,6f,20,80,5,8d,40,1d,41,33,b7,20,0,85,43,b7,4,8,0,91,4,5,4,63,4,77,0,6f,20,e0,
  //   3,9d,40,d,41,33,b7,20,0,81,43,b7,4,8,0,95,4,5,4,63,4,77,0,6f,20,40,2,81,40,37,81,
  //   ff,ff,33,b7,20,0,85,43,b7,4,8,0,99,4,5,4,63,4,77,0,6f,20,80,0,b7,0,0,80,1,41,33,b7,
  //   20,0,81,43,b7,4,8,0,9d,4,5,4,63,4,77,0,6f,10,d0,7e,b7,0,0,80,37,81,ff,ff,33,b7,20,
  //   0,85,43,b7,4,8,0,a1,4,5,4,63,4,77,0,6f,10,f0,7c,81,40,37,81,0,0,7d,11,33,b7,20,0,
  //   85,43,b7,4,8,0,a5,4,5,4,63,4,77,0,6f,10,10,7b,b7,0,0,80,fd,10,1,41,33,b7,20,0,81,
  //   43,b7,4,8,0,a9,4,5,4,63,4,77,0,6f,10,30,79,b7,0,0,80,fd,10,37,81,0,0,7d,11,33,b7,
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  //   PC
  //   Opcode
  //   Microcode
  //   contents of MicroCode (hex, n*v repeats v):
  //   32a32e43,32a32e43,32a32e43,32a32e43,32a32e43,32a32e43,32a32e43,32a32e43,a30ec1,a30f41,
  //   a30c41,a30e43,a30f43,a30c41,a30e43,a30f43,a30c41,a30e43,a30f43,a30c41,a30e43,a30e43,
  //   a30e49,a10e49,8a30e4b,8a30e4b,8a30e4b,8a30e4b,8a30e4b,8a30e4b,8a30e4b,8a30e4b,a30ec9,
  //   a30f49,a30c49,40a3064b,40a3064b,40a3064b,40a3064b,40a3064b,40a3064b,40a3064b,40a3064b,
  //   40a30668,0,0,0,0,0,0,0,0,0,0,0,0,0,0,0,0,0,0,0,0,32a32e43,32a32e43,32a32e43,32a32e43,
  //   32a32e43,32a32e43,32a32e43,32a32e43,a30ec1,a30f41,a30c41,a30e43,a30f43,a30c41,a30e43,
  //   a30f43,a30c41,a30e43,a30f43,a30c41,a30e43,a30e43,a30e49,a30e49,a30e09,a30e08,0,0,
  //   0,0,0,0,0,0,0,0,0,0,0,0,0,0,0,0,0,0,0,0,0,0,0,0,0,0,0,0,0,0,0,0,0,0,0,0,32a32e43,
  //   32a32e43,32a32e43,32a32e43,32a32e43,32a32e43,32a32e43,32a32e43,a30ec1,a30f41,a30c41,
  //   a30e43,a30f43,a30c41,a30e43,a30f43,a30c41,a30e43,a30f43,a30c41,a30e43,a30e43,a30e49,
  //   a30e49,a30e09,a30e08,0,0,0,0,0,0,0,0,0,0,0,0,0,0,0,0,0,0,0,0,0,0,0,0,0,0,0,0,0,0,
  //   0,0,0,0,0,0,0,0,32a32e43,32a32e43,32a32e43,32a32e43,32a32e43,32a32e43,32a32e43,32a32e43,
  //   a30ec1,a30f41,a30c41,a30e43,a30f43,a30c41,a30e43,a30f43,a30c41,a30e43,a30f43,a30c41,
  //   a30e43,a30e43,a30e49,a30e49,a30e68,0,0,0,0,0,0,0,0,0,0,0,0,0,0,0,0,0,0,0,0,0,0,0,
  //   0,0,0,0,0,0,0,0,0,0,0,0,0,0,0,0,32a32e43,32a32e43,32a32e43,32a32e43,32a32e43,32a32e43,
  //   32a32e43,32a32e43,a30ec1,a30f41,a30c41,a30e43,a30f43,a30c41,a30e43,a30f43,a30c41,
  //   a30e43,a30f43,a30c41,a30e43,a30e43,a30e49,a10e49,8a3064b,8a3064b,8a3064b,8a3064b,
  //   8a3064b,8a3064b,8a3064b,8a3064b,a30e68,0,0,0,0,0,0,0,0,0,0,0,0,0,0,0,0,0,0,0,0,0,
  //   0,0,0,0,0,0,0,0,0,0,32a32e43,32a32e43,32a32e43,32a32e43,32a32e43,32a32e43,32a32e43,
  //   32a32e43,a30ec1,a30f41,a30c41,a30e43,a30f43,a30c41,a30e43,a30f43,a30c41,a30e43,a30f43,
  //   a30c41,a30e43,a30e43,a30e49,a10e49,22a3064b,22a3064b,22a3064b,22a3064b,22a3064b,22a3064b,
  //   22a3064b,22a3064b,a30e68,0,0,0,0,0,0,0,0,0,0,0,0,0,0,0,0,0,0,0,0,0,0,0,0,0,0,0,0,
  //   0,0,0,32a32e43,32a32e43,32a32e43,32a32e43,32a32e43,32a32e43,32a32e43,32a32e43,a30ec1,
  //   a30f41,a30c41,a30e43,a30f43,a30c41,a30e43,a30f43,a30c41,a30e43,a30f43,a30c41,a30e43,
  //   a30e43,a30e49,a30e49,a30e09,a30e08,0,0,0,0,0,0,0,0,0,0,0,0,0,0,0,0,0,0,0,0,0,0,0,
  //   0,0,0,0,0,0,0,0,0,0,0,0,0,0,0,32a32e43,32a32e43,32a32e43,32a32e43,32a32e43,32a32e43,
  //   32a32e43,32a32e43,a30ec1,a30f41,a30c41,a30e43,a30f43,a30c41,a30e43,a30f43,a30c41,
  //   a30e43,a30f43,a30c41,a30e43,a30e43,a30e49,a30e49,a30e09,a30e08,0,0,0,0,0,0,0,0,0,
  //   0,0,0,0,0,0,0,0,0,0,0,0,0,0,0,0,0,0,0,0,0,0,0,0,0,0,0,0,0,32a32e43,32a32e43,32a32e43,
  //   32a32e43,32a32e43,32a32e43,32a32e43,32a32e43,a30ec1,a30f41,a30c41,a30e43,a30f43,a30c41,
  //   a30e43,a30f43,a30c41,a30e43,a30f43,a30c41,a30e43,a30e43,a30e49,a10e49,10a30e4b,10a30e4b,
  //   10a30e4b,10a30e4b,10a30e4b,10a30e4b,10a30e4b,10a30e4b,a30ecb,a30f4b,a30a49,a30a4b,
  //   a30a4b,a30a4b,a30a4b,a30a4b,a30a4b,a30e68,0,0,0,0,0,0,0,0,0,0,0,0,0,0,0,0,0,0,0,0,
  //   0,0,32a32e43,32a32e43,32a32e43,32a32e43,32a32e43,32a32e43,32a32e43,32a32e43,a30ec1,
  //   a30f41,a30c41,a30e43,a30f43,a30c41,a30e43,a30f43,a30c41,a30e43,a30f43,a30c41,a30e43,
  //   a30e43,a30e49,a30e49,a30e09,a30e08,0,0,0,0,0,0,0,0,0,0,0,0,0,0,0,0,0,0,0,0,0,0,0,
  //   0,0,0,0,0,0,0,0,0,0,0,0,0,0,0,32a32e43,32a32e43,32a32e43,32a32e43,32a32e43,32a32e43,
  //   32a32e43,32a32e43,a30ec1,a30f41,a30c41,a30e43,a30f43,a30c41,a30e43,a30f43,a30c41,
  //   a30e43,a30f43,a30c41,a30e43,a30e43,a30e49,a30e49,a30e09,a30e08,0,0,0,0,0,0,0,0,0,
  //   0,0,0,0,0,0,0,0,0,0,0,0,0,0,0,0,0,0,0,0,0,0,0,0,0,0,0,0,0,32a32e43,32a32e43,32a32e43,
  //   32a32e43,32a32e43,32a32e43,32a32e43,32a32e43,a30ec1,a30f41,a30c41,a30e43,a30f43,a30c41,
  //   a30e43,a30f43,a30c41,a30e43,a30f43,a30c41,a30e43,a30e43,a30e49,a30e49,a30e09,a30e08,
  //   0,0,0,0,0,0,0,0,0,0,0,0,0,0,0,0,0,0,0,0,0,0,0,0,0,0,0,0,0,0,0,0,0,0,0,0,0,0,32a32e43,
  //   32a32e43,32a32e43,32a32e43,32a32e43,32a32e43,32a32e43,32a32e43,a30ec1,a30f41,a30c41,
  //   a30e43,a30f43,a30c41,a30e43,a30f43,a30c41,a30e43,a30f43,a30c41,a30e43,a30e43,a30e49,
  //   a10e49,a3064b,a3064b,a3064b,a3064b,a3064b,a3064b,a3064b,a3064b,a30e68,0,0,0,0,0,0,
  //   0,0,0,0,0,0,0,0,0,0,0,0,0,0,0,0,0,0,0,0,0,0,0,0,0,32a32e43,32a32e43,32a32e43,32a32e43,
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  //   Registers
  //   CSR
endmodule
