// Digital circuit CSR-address.dig as structural Verilog
module CSR_address (
  input  CLK,
  input  IN,
  input  LATCH,
  input  nRESET,
  output [11:0] OUT
);

  wire _74hc595_2_qh_2;

  _74HC595 _74hc595_1 (
    .SER(_74hc595_2_qh_2), .SRCLK(CLK), .nSRCLR(nRESET), .RCLK(LATCH), .nOE(1'b0), .VCC(1'b1), .GND(1'b0),
    .QH(OUT[0]), .QG(OUT[1]), .QF(OUT[2]), .QE(OUT[3]), .QD(OUT[4]), .QC(OUT[5]), .QB(OUT[6]), .QA(OUT[7]));  // open: QH_2
  _74HC595 _74hc595_2 (
    .SER(IN), .SRCLK(CLK), .nSRCLR(nRESET), .RCLK(LATCH), .nOE(1'b0), .VCC(1'b1), .GND(1'b0), .QH(OUT[8]),
    .QG(OUT[9]), .QF(OUT[10]), .QE(OUT[11]), .QH_2(_74hc595_2_qh_2));  // open: QD, QC, QB, QA
endmodule
