// Digital circuit Clock-driver.dig as structural Verilog
module Clock_driver (
  input  CLK_RAW,
  input  Stop,
  input  Run,
  input  One_Instruction,
  input  One_Step,
  input  One_Substep,
  input  STEPDONE,
  input  OPDONE,
  input  RESET,
  input  WAKEUP,
  input  nSLEEP,
  input  nWAIT,
  output CLK,
  output nCLK,
  output LED_R,
  output LED_G
);

  wire _74hc4017_1_q0, _74hc4017_1_q1, _74hc4017_1_q2, _74hc4017_1_q4, _74hc4017_1_q5, _74hc4017_1_q7,
       _74hc4017_1_q8, _74hc4017_1_q9, and_1_out, d_ff_as_1_q, d_ff_as_2_q, d_ff_as_3_q, d_ff_as_4_q,
       d_ff_as_5_q, diodebackward_1_out, diodebackward_2_out, diodebackward_3_out, diodeforward_1_out,
       nand_1_out, nand_2_out, nand_3_out, nand_4_out, nand_6_out, nor_1_out, not_1_out, not_2_out, or_1_out,
       pullup_4_out, Q3, Q5;

  nand nand_1 (nand_1_out, Q5, STEPDONE);
  nand nand_2 (nand_2_out, Q5, OPDONE);
  not not_1 (not_1_out, Q5);
  // RGBLED rgbled_1: pin names not known; wires that end beside it: LED_R, LED_G, 1'b0
  DiodeBackward diodebackward_1 (.in(not_1_out), .out(diodebackward_1_out));
  DiodeBackward diodebackward_2 (.in(nand_1_out), .out(diodebackward_2_out));
  DiodeBackward diodebackward_3 (.in(nand_2_out), .out(diodebackward_3_out));
  PullUp pullup_1 (.out(diodebackward_1_out));
  PullUp pullup_2 (.out(diodebackward_2_out));
  PullUp pullup_3 (.out(diodebackward_3_out));
  PullUp pullup_4 (.out(pullup_4_out));
  DiodeBackward diodebackward_4 (.in(Stop), .out(diodebackward_1_out));
  DiodeBackward diodebackward_5 (.in(Stop), .out(diodebackward_2_out));
  DiodeBackward diodebackward_6 (.in(Stop), .out(diodebackward_3_out));
  DiodeBackward diodebackward_7 (.in(Stop), .out(pullup_4_out));
  nor nor_1 (nor_1_out, WAKEUP, RESET);
  DiodeBackward diodebackward_8 (.in(One_Instruction), .out(pullup_4_out));
  DiodeBackward diodebackward_9 (.in(One_Step), .out(diodebackward_3_out));
  DiodeBackward diodebackward_10 (.in(One_Step), .out(pullup_4_out));
  D_FF_AS #(.Default(1)) d_ff_as_1 (.Set(~nor_1_out), .D(nSLEEP), .C(Q3), .Clr(1'b0), .Q(d_ff_as_1_q));  // open: nQ
  DiodeBackward diodebackward_11 (.in(One_Substep), .out(diodebackward_2_out));
  DiodeBackward diodebackward_12 (.in(One_Substep), .out(diodebackward_3_out));
  DiodeBackward diodebackward_13 (.in(One_Substep), .out(pullup_4_out));
  not not_2 (not_2_out, RESET);
  D_FF_AS d_ff_as_2 (.Set(~1'b1), .D(1'b1), .C(~One_Substep), .Clr(~diodebackward_1_out), .Q(d_ff_as_2_q));  // open: nQ
  DiodeBackward diodebackward_14 (.in(not_2_out), .out(diodebackward_1_out));
  D_FF_AS d_ff_as_3 (.Set(~1'b1), .D(1'b1), .C(~One_Step), .Clr(~diodebackward_2_out), .Q(d_ff_as_3_q));  // open: nQ
  DiodeBackward diodebackward_15 (.in(not_2_out), .out(diodebackward_2_out));
  D_FF_AS d_ff_as_4 (
    .Set(~1'b1), .D(1'b1), .C(~One_Instruction), .Clr(~diodebackward_3_out), .Q(d_ff_as_4_q));  // open: nQ
  DiodeBackward diodebackward_16 (.in(not_2_out), .out(diodebackward_3_out));
  D_FF_AS d_ff_as_5 (.Set(~1'b1), .D(1'b1), .C(~Run), .Clr(~pullup_4_out), .Q(d_ff_as_5_q));  // open: nQ
  DiodeBackward diodebackward_17 (.in(not_2_out), .out(pullup_4_out));
  and and_1 (and_1_out, d_ff_as_1_q, nWAIT);
  DiodeForward diodeforward_1 (.in(d_ff_as_2_q), .out(diodeforward_1_out));
  DiodeForward diodeforward_2 (.in(d_ff_as_3_q), .out(diodeforward_1_out));
  DiodeForward diodeforward_3 (.in(d_ff_as_4_q), .out(diodeforward_1_out));
  DiodeForward diodeforward_4 (.in(d_ff_as_5_q), .out(diodeforward_1_out));
  _74HC4017 _74hc4017_1 (
    .CLK(CLK_RAW), .nEN(LED_R), .MR(RESET), .Q0(_74hc4017_1_q0), .Q1(_74hc4017_1_q1), .Q2(_74hc4017_1_q2),
    .Q3(Q3), .Q4(_74hc4017_1_q4), .Q5(_74hc4017_1_q5), .Q6(Q5), .Q7(_74hc4017_1_q7), .Q8(_74hc4017_1_q8),
    .Q9(_74hc4017_1_q9));  // open: nQ59
  PullDown pulldown_1 (.out(diodeforward_1_out));
  nand nand_3 (nand_3_out, diodeforward_1_out, _74hc4017_1_q0);
  nand nand_4 (nand_4_out, nand_3_out, _74hc4017_1_q0);
  or or_1 (or_1_out, _74hc4017_1_q9, RESET);
  nand nand_5 (LED_G, nand_3_out, nand_6_out);
  nand nand_6 (nand_6_out, LED_G, nand_4_out);
  RS_FF_AS rs_ff_as_1 (.S(_74hc4017_1_q0), .R(_74hc4017_1_q4), .Q(nCLK));  // open: nQ
  RS_FF_AS rs_ff_as_2 (.S(_74hc4017_1_q5), .R(or_1_out), .Q(CLK));  // open: nQ
  nand nand_7 (LED_R, and_1_out, LED_G);

  // Other names for the same wires on the sheet: nCLK_EN = LED_R; RAWCLK = CLK_RAW

  // Notes on the sheet:
  //   CLK_RAW: Hz: 2
  //   Stop: default 1
  //   Run: default 1
  //   One_Instruction: default 1
  //   One_Step: default 1
  //   One_Substep: default 1
  //   STEPDONE: default 1
  //   OPDONE: default 1
  //   nSLEEP: default 1
  //   nWAIT: default 1
endmodule
