// Digital circuit Clock.dig as structural Verilog
module Clock (
  input  CLK,
  input  nCLK,
  input  nLEN8,
  input  LASTSTEP,
  input  nRESET,
  output [5:0] STEP,
  output STEPDONE,
  output [7:0] SUBSTEP,
  output OPDONE
);

  wire and_1_out, nOPDONE, not_1_out, substep_counter_1_last_substep, substep_counter_1_nstep_done,
       switchdt_1_p3;

  not not_1 (not_1_out, CLK);
  // SwitchDT switchdt_1: pin names not known; wires that end beside it: nCLK, not_1_out, switchdt_1_p3
  Substep_Counter substep_counter_1 (
    .nCLK(switchdt_1_p3), .CLK(CLK), .nLEN4(nLEN8), .EN(nRESET),
    .LAST_SUBSTEP(substep_counter_1_last_substep), .nSTEP_DONE(substep_counter_1_nstep_done), .DVAL(SUBSTEP),
    .STEP_DONE(STEPDONE));  // open: nRESET
  Step_Counter step_counter_1 (.nCLK(switchdt_1_p3), .nRESET(nRESET), .EN(STEPDONE), .nOPDONE(nOPDONE), .COUNT(STEP));
  and and_1 (and_1_out, substep_counter_1_last_substep, LASTSTEP);
  D_FF d_ff_1 (.D(and_1_out), .C(CLK), .Q(OPDONE), .nQ(nOPDONE));

  // Notes on the sheet:
  //   LASTSTEP: default 1
endmodule

/* Test case:
CLK ~CLK ~RESET ~LEN4 LASTSTEP STEP SUBSTEP ~STEPDONE ~OPDONE

0 1 0 1 0 X X X X
0 1 1 1 0 X X X X
0 1 1 0 0 0 0 X 1
1 0 1 0 0 0 0 1 1
0 1 1 0 0 0 1 1 1
1 0 1 0 0 0 1 1 1
0 1 1 0 0 0 2 1 1
1 0 1 0 0 0 2 1 1
0 1 1 0 0 0 3 1 1
1 0 1 0 0 0 3 0 1
0 1 1 0 0 1 0 0 1
1 0 1 0 0 1 0 1 1
0 1 1 0 0 1 1 1 1
1 0 1 0 0 1 1 1 1
0 1 1 0 0 1 2 1 1
1 0 1 0 0 1 2 1 1
0 1 1 0 0 1 3 1 1
1 0 1 0 0 1 3 0 1
0 1 1 0 0 2 0 0 1
1 0 1 0 0 2 0 1 1
0 1 1 0 0 2 1 1 1
1 0 1 0 0 2 1 1 1
0 1 1 0 0 2 2 1 1
1 0 1 0 0 2 2 1 1
0 1 1 0 0 2 3 1 1
1 0 1 0 0 2 3 0 1
0 1 1 0 0 3 0 0 1
1 0 1 0 0 3 0 1 1
0 1 1 0 0 3 1 1 1
1 0 1 0 0 3 1 1 1
0 1 1 0 0 3 2 1 1
1 0 1 0 0 3 2 1 1
0 1 1 0 0 3 3 1 1
1 0 1 0 0 3 3 0 1
0 1 1 0 0 4 0 0 1
1 0 1 0 0 4 0 1 1
0 1 1 0 0 4 1 1 1
1 0 1 0 0 4 1 1 1
0 1 1 0 0 4 2 1 1
1 0 1 0 0 4 2 1 1
0 1 1 0 0 4 3 1 1
1 0 1 0 0 4 3 0 1
0 1 1 0 0 5 0 0 1
1 0 1 0 0 5 0 1 1
0 1 1 0 0 5 1 1 1
1 0 1 0 0 5 1 1 1
0 1 1 0 0 5 2 1 1
1 0 1 0 0 5 2 1 1
0 1 1 0 0 5 3 1 1
1 0 1 0 0 5 3 0 1
0 1 1 0 0 6 0 0 1
1 0 1 0 0 6 0 1 1
0 1 1 0 0 6 1 1 1
1 0 1 0 0 6 1 1 1
0 1 1 0 0 6 2 1 1
1 0 1 0 0 6 2 1 1
0 1 1 0 0 6 3 1 1
1 0 1 0 0 6 3 0 1
0 1 1 0 0 7 0 0 1
1 0 1 0 0 7 0 1 1
0 1 1 0 0 7 1 1 1
1 0 1 0 0 7 1 1 1
0 1 1 0 0 7 2 1 1
1 0 1 0 0 7 2 1 1
0 1 1 0 0 7 3 1 1
1 0 1 0 0 7 3 0 1
0 1 1 1 0 8 0 0 1
1 0 1 1 0 8 0 0 1
0 1 1 1 0 9 0 0 1
1 0 1 1 0 9 0 0 1
0 1 1 1 0 10 0 0 1
1 0 1 1 0 10 0 0 1
0 1 1 0 0 11 0 0 1
1 0 1 0 0 11 0 1 1
0 1 1 0 0 11 1 1 1
1 0 1 0 0 11 1 1 1
0 1 1 0 0 11 2 1 1
1 0 1 0 0 11 2 1 1
0 1 1 0 0 11 3 1 1
1 0 1 0 0 11 3 0 1
0 1 1 0 0 12 0 0 1
1 0 1 0 0 12 0 1 1
0 1 1 0 0 12 1 1 1
1 0 1 0 0 12 1 1 1
0 1 1 0 0 12 2 1 1
1 0 1 0 0 12 2 1 1
0 1 1 0 0 12 3 1 1
1 0 1 0 0 12 3 0 1
0 1 1 1 0 13 0 0 1
1 0 1 1 0 13 0 0 1
0 1 1 0 0 14 0 0 1
1 0 1 0 0 14 0 1 1
0 1 1 0 0 14 1 1 1
1 0 1 0 0 14 1 1 1
0 1 1 0 0 14 2 1 1
1 0 1 0 0 14 2 1 1
0 1 1 0 0 14 3 1 1
1 0 1 0 0 14 3 0 1
0 1 1 0 0 15 0 0 1
1 0 1 0 0 15 0 1 1
0 1 1 0 0 15 1 1 1
1 0 1 0 0 15 1 1 1
0 1 1 0 0 15 2 1 1
1 0 1 0 0 15 2 1 1
0 1 1 0 0 15 3 1 1
1 0 1 0 0 15 3 0 1
0 1 1 1 0 16 0 0 1
1 0 1 1 0 16 0 0 1
0 1 1 0 0 17 0 0 1
1 0 1 0 0 17 0 1 1
0 1 1 0 0 17 1 1 1
1 0 1 0 0 17 1 1 1
0 1 1 0 0 17 2 1 1
1 0 1 0 0 17 2 1 1
0 1 1 0 0 17 3 1 1
1 0 1 0 0 17 3 0 1
0 1 1 0 0 18 0 0 1
1 0 1 0 0 18 0 1 1
0 1 1 0 0 18 1 1 1
1 0 1 0 0 18 1 1 1
0 1 1 0 0 18 2 1 1
1 0 1 0 0 18 2 1 1
0 1 1 0 0 18 3 1 1
1 0 1 0 0 18 3 0 1
0 1 1 1 0 19 0 0 1
1 0 1 1 0 19 0 0 1
0 1 1 0 0 20 0 0 1
1 0 1 0 0 20 0 1 1
0 1 1 0 0 20 1 1 1
1 0 1 0 0 20 1 1 1
0 1 1 0 0 20 2 1 1
1 0 1 0 0 20 2 1 1
0 1 1 0 0 20 3 1 1
1 0 1 0 0 20 3 0 1
0 1 1 0 0 21 0 0 1
1 0 1 0 0 21 0 1 1
0 1 1 0 0 21 1 1 1
1 0 1 0 0 21 1 1 1
0 1 1 0 0 21 2 1 1
1 0 1 0 0 21 2 1 1
0 1 1 0 0 21 3 1 1
1 0 1 0 0 21 3 0 1
0 1 1 1 0 22 0 0 1
1 0 1 1 0 22 0 0 1
0 1 1 1 0 23 0 0 1
1 0 1 1 0 23 0 0 1
0 1 1 0 0 24 0 0 1
1 0 1 0 0 24 0 1 1
0 1 1 0 0 24 1 1 1
1 0 1 0 0 24 1 1 1
0 1 1 0 0 24 2 1 1
1 0 1 0 0 24 2 1 1
0 1 1 0 0 24 3 1 1
1 0 1 0 0 24 3 0 1
0 1 1 0 0 25 0 0 1
1 0 1 0 0 25 0 1 1
0 1 1 0 0 25 1 1 1
1 0 1 0 0 25 1 1 1
0 1 1 0 0 25 2 1 1
1 0 1 0 0 25 2 1 1
0 1 1 0 0 25 3 1 1
1 0 1 0 0 25 3 0 1
0 1 1 0 0 26 0 0 1
1 0 1 0 0 26 0 1 1
0 1 1 0 0 26 1 1 1
1 0 1 0 0 26 1 1 1
0 1 1 0 0 26 2 1 1
1 0 1 0 0 26 2 1 1
0 1 1 0 0 26 3 1 1
1 0 1 0 0 26 3 0 1
0 1 1 0 0 27 0 0 1
1 0 1 0 0 27 0 1 1
0 1 1 0 0 27 1 1 1
1 0 1 0 0 27 1 1 1
0 1 1 0 0 27 2 1 1
1 0 1 0 0 27 2 1 1
0 1 1 0 0 27 3 1 1
1 0 1 0 0 27 3 0 1
0 1 1 0 0 28 0 0 1
1 0 1 0 0 28 0 1 1
0 1 1 0 0 28 1 1 1
1 0 1 0 0 28 1 1 1
0 1 1 0 0 28 2 1 1
1 0 1 0 0 28 2 1 1
0 1 1 0 0 28 3 1 1
1 0 1 0 0 28 3 0 1
0 1 1 0 0 29 0 0 1
1 0 1 0 0 29 0 1 1
0 1 1 0 0 29 1 1 1
1 0 1 0 0 29 1 1 1
0 1 1 0 0 29 2 1 1
1 0 1 0 0 29 2 1 1
0 1 1 0 0 29 3 1 1
1 0 1 0 0 29 3 0 1
0 1 1 0 0 30 0 0 1
1 0 1 0 0 30 0 1 1
0 1 1 0 0 30 1 1 1
1 0 1 0 0 30 1 1 1
0 1 1 0 0 30 2 1 1
1 0 1 0 0 30 2 1 1
0 1 1 0 0 30 3 1 1
1 0 1 0 0 30 3 0 1
0 1 1 0 0 31 0 0 1
1 0 1 0 0 31 0 1 1
0 1 1 0 0 31 1 1 1
1 0 1 0 0 31 1 1 1
0 1 1 0 0 31 2 1 1
1 0 1 0 0 31 2 1 1
0 1 1 0 0 31 3 1 1
1 0 1 0 0 31 3 0 1
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*/
