// Digital circuit Imm16.dig as structural Verilog
module Imm16 (
  input  CLK,
  input  nRESET,
  input  LATCH,
  input  SnP,
  input  [15:0] Val,
  output OUT,
  output [15:0] DVal
);

  wire _74597_1_p14;

  // _74597 _74597_1: pin names not known; wires that end beside it: nRESET, CLK, Val[15], LATCH, SnP, Val[8], Val[9], Val[10], Val[11], Val[12], Val[13], Val[14], Val[15], _74597_1_p14, DVal[15:8]
  // _74597 _74597_2: pin names not known; wires that end beside it: nRESET, CLK, _74597_1_p14, LATCH, SnP, Val[0], Val[1], Val[2], Val[3], Val[4], Val[5], Val[6], Val[7], OUT, DVal[7:0]
endmodule
