// Digital circuit Imm32.dig as structural Verilog
module Imm32 (
  input  CLK,
  input  nRESET,
  input  LATCH,
  input  SnP,
  input  [31:0] Val,
  output OUT
);

  wire _74597_1_p14, _74597_2_p14, _74597_3_p14;

  // _74597 _74597_1: pin names not known; wires that end beside it: nRESET, CLK, Val[31], LATCH, SnP, Val[24], Val[25], Val[26], Val[27], Val[28], Val[29], Val[30], Val[31], _74597_1_p14
  // _74597 _74597_2: pin names not known; wires that end beside it: nRESET, CLK, _74597_1_p14, LATCH, SnP, Val[16], Val[17], Val[18], Val[19], Val[20], Val[21], Val[22], Val[23], _74597_2_p14
  // _74597 _74597_3: pin names not known; wires that end beside it: nRESET, CLK, _74597_2_p14, LATCH, SnP, Val[8], Val[9], Val[10], Val[11], Val[12], Val[13], Val[14], Val[15], _74597_3_p14
  // _74597 _74597_4: pin names not known; wires that end beside it: nRESET, CLK, _74597_3_p14, LATCH, SnP, Val[0], Val[1], Val[2], Val[3], Val[4], Val[5], Val[6], Val[7], OUT
endmodule
