// Digital circuit Imm8.dig as structural Verilog
module Imm8 (
  input  CLK,
  input  nRESET,
  input  LATCH,
  input  SnP,
  input  [7:0] Val,
  output OUT
);

  // _74597 _74597_1: pin names not known; wires that end beside it: nRESET, CLK, Val[7], LATCH, SnP, Val[0], Val[1], Val[2], Val[3], Val[4], Val[5], Val[6], Val[7], OUT
endmodule
