// Digital circuit Interrupt-Controller.dig as structural Verilog
module Interrupt_Controller (
  input  BUS_CLK,
  input  IRQ_OP_SnP,
  input  LASTSTEP,
  input  nIRQ,
  input  OP_LATCH,
  input  nRESET,
  output IRQ_OP,
  output IRQ_OP_FETCH
);

  wire diodebackward_1_out, not_1_out, not_2_out;

  not not_1 (not_1_out, OP_LATCH);
  not not_2 (not_2_out, LASTSTEP);
  DiodeBackward diodebackward_1 (.in(nRESET), .out(diodebackward_1_out));
  DiodeBackward diodebackward_2 (.in(not_1_out), .out(diodebackward_1_out));
  PullUp pullup_1 (.out(diodebackward_1_out));
  D_FF_AS #(.Default(1)) d_ff_as_1 (
    .Set(~diodebackward_1_out), .D(nIRQ), .C(not_2_out), .Clr(~1'b1), .nQ(IRQ_OP_FETCH));  // open: Q
  Imm32 u_irq_op (.CLK(BUS_CLK), .nRESET(nRESET), .LATCH(BUS_CLK), .SnP(IRQ_OP_SnP), .Val(32'h300073), .OUT(IRQ_OP));
endmodule
