// Digital circuit MCAUSE.dig as structural Verilog
module MCAUSE (
  input  BUS_CLK,
  input  CSR_IN_LATCH,
  input  CSR_OUT_LATCH,
  input  [11:0] CSR_ADDR,
  input  [1:0] TRAP2,
  input  nIRQ,
  input  INT1P,
  input  INT2P,
  input  INT3P,
  input  IRQ_LATCH,
  input  nRESET,
  output CSR_OUT,
  output [31:0] mcause
);

  wire _74597_1_p14, _74597_2_p14, _74597_3_p14, _74597_4_p14, and_1_out, comparator_1_eq, decoder_1_out_3,
       EBREAK, ECALL, IllOp, IN_LATCH, IRQ, MRET, nand_1_out, nor_1_out, not_1_out, not_3_out, nPL;

  Comparator #(.Bits(12)) comparator_1 (.a(CSR_ADDR), .b(12'h342), .eq(comparator_1_eq));  // open: gt, lt
  not not_1 (not_1_out, comparator_1_eq);
  or or_1 (IN_LATCH, not_1_out, CSR_IN_LATCH);
  Decoder #(.Selector_Bits(2)) decoder_1 (
    .sel(TRAP2), .out_0(ECALL), .out_1(EBREAK), .out_2(MRET), .out_3(decoder_1_out_3));
  not not_2 (nPL, IN_LATCH);
  Demultiplexer demultiplexer_1 (.sel(nIRQ), .in(decoder_1_out_3), .out_0(IRQ), .out_1(IllOp));
  not not_3 (not_3_out, INT1P);
  and and_1 (and_1_out, IRQ, not_3_out, INT2P);
  nand nand_1 (nand_1_out, IRQ, INT1P);
  nor nor_1 (nor_1_out, and_1_out, IllOp);
  D_FF_AS d_ff_as_1 (.Set(~1'b1), .D(IRQ), .C(IRQ_LATCH), .Clr(~nRESET), .Q(mcause[31]));  // open: nQ
  D_FF_AS d_ff_as_2 (.Set(~1'b1), .D(ECALL), .C(IRQ_LATCH), .Clr(~nRESET), .Q(mcause[3]));  // open: nQ
  D_FF_AS d_ff_as_3 (.Set(~1'b1), .D(nand_1_out), .C(IRQ_LATCH), .Clr(~nRESET), .Q(mcause[1]));  // open: nQ
  D_FF_AS d_ff_as_4 (.Set(~1'b1), .D(nor_1_out), .C(IRQ_LATCH), .Clr(~nRESET), .Q(mcause[0]));  // open: nQ
  // _74597 _74597_1: pin names not known; wires that end beside it: nRESET, BUS_CLK, 1'b0, CSR_OUT_LATCH, nPL, 1'b0, 1'b0, 1'b0, 1'b0, 1'b0, 1'b0, 1'b0, mcause[31], _74597_1_p14
  // _74597 _74597_2: pin names not known; wires that end beside it: nRESET, BUS_CLK, _74597_1_p14, CSR_OUT_LATCH, nPL, 1'b0, 1'b0, 1'b0, 1'b0, 1'b0, 1'b0, 1'b0, 1'b0, _74597_2_p14
  // _74597 _74597_3: pin names not known; wires that end beside it: nRESET, BUS_CLK, _74597_2_p14, CSR_OUT_LATCH, nPL, 1'b0, 1'b0, 1'b0, 1'b0, 1'b0, 1'b0, 1'b0, 1'b0, _74597_3_p14
  // _74597 _74597_4: pin names not known; wires that end beside it: nRESET, BUS_CLK, _74597_3_p14, CSR_OUT_LATCH, nPL, mcause[0], mcause[1], 1'b0, mcause[3], mcause[31], 1'b0, 1'b0, 1'b0, _74597_4_p14
  assign CSR_OUT = ~IN_LATCH ? _74597_4_p14 : 1'bz;  // DriverInvSel driverinvsel_1

  assign {mcause[30:4], mcause[2]} = {{26{1'b0}}, mcause[31], 1'b0};

  // Other names for the same wires on the sheet: B0 = mcause[0]; B1 = mcause[1]; B3 = mcause[3]; B4 = mcause[31];
  //   B31 = mcause[31]; BIT_LATCH = IRQ_LATCH

  // Notes on the sheet:
  //   TRAP2:
  //   00 ECALL
  //   01 EBREAK
  //   10 MRET
  //   11 Interrupt/Illegal Operation
  //   mcause:
  //   0x00000002  Illegal Instruction
  //   0x00000003  EBREAK
  //   0x0000000B  ECALL
  //   0x80000011  Interrupt #1
  //   0x80000012  Interrupt #2
  //   0x80000013  Interrupt #3
endmodule
