// Digital circuit MIE.dig as structural Verilog
module MIE (
  input  CLK,
  input  BUS_CLK,
  input  CSR_IN,
  input  CSR_IN_LATCH,
  input  CSR_OUT_LATCH,
  input  [11:0] CSR_ADDR,
  input  nRESET,
  output CSR_OUT,
  output [31:0] mie,
  output MEI1E,
  output MEI2E,
  output MEI3E
);

  wire _74595_1_p8, _74595_2_p11, _74595_3_p8, _74597_1_p14, _74597_2_p14, _74597_3_p14, BIT_LATCH,
       comparator_1_eq, IN_LATCH, not_1_out, nPL;

  Comparator #(.Bits(12)) comparator_1 (.a(CSR_ADDR), .b(12'h304), .eq(comparator_1_eq));  // open: gt, lt
  not not_1 (not_1_out, comparator_1_eq);
  D_FF_AS d_ff_as_1 (.Set(~nRESET), .D(IN_LATCH), .C(CLK), .Clr(~1'b1), .Q(BIT_LATCH));  // open: nQ
  or or_1 (IN_LATCH, not_1_out, CSR_IN_LATCH);
  not not_2 (nPL, IN_LATCH);
  // _74595 _74595_1: pin names not known; wires that end beside it: CSR_IN, BUS_CLK, nRESET, IN_LATCH, 1'b0, 1'b1, 1'b0, _74595_1_p8
  // _74595 _74595_2: pin names not known; wires that end beside it: _74595_1_p8, BUS_CLK, nRESET, IN_LATCH, 1'b0, 1'b1, 1'b0, MEI1E, MEI2E, MEI3E, _74595_2_p11
  // _74595 _74595_3: pin names not known; wires that end beside it: _74595_2_p11, BUS_CLK, nRESET, IN_LATCH, 1'b0, 1'b1, 1'b0, _74595_3_p8
  // _74595 _74595_4: pin names not known; wires that end beside it: _74595_3_p8, BUS_CLK, nRESET, IN_LATCH, 1'b0, 1'b1, 1'b0
  // _74597 _74597_1: pin names not known; wires that end beside it: nRESET, BUS_CLK, 1'b0, CSR_OUT_LATCH, nPL, 1'b0, MEI1E, MEI2E, MEI3E, 1'b0, 1'b0, 1'b0, 1'b0, _74597_1_p14
  // _74597 _74597_2: pin names not known; wires that end beside it: nRESET, BUS_CLK, _74597_1_p14, CSR_OUT_LATCH, nPL, 1'b0, 1'b0, 1'b0, 1'b0, 1'b0, 1'b0, 1'b0, 1'b0, _74597_2_p14
  // _74597 _74597_3: pin names not known; wires that end beside it: nRESET, BUS_CLK, _74597_2_p14, CSR_OUT_LATCH, nPL, 1'b0, 1'b0, 1'b0, 1'b0, 1'b0, 1'b0, 1'b0, 1'b0, _74597_3_p14
  assign CSR_OUT = ~IN_LATCH ? _74597_3_p14 : 1'bz;  // DriverInvSel driverinvsel_1

  assign mie = {{12{1'b0}}, MEI3E, MEI2E, MEI1E, {17{1'b0}}};
endmodule
