// Digital circuit MIP.dig as structural Verilog
module MIP (
  input  CLK,
  input  BUS_CLK,
  input  CSR_IN,
  input  CSR_IN_LATCH,
  input  CSR_OUT_LATCH,
  input  [11:0] CSR_ADDR,
  input  nINT1,
  input  nINT2,
  input  nINT3,
  input  nRESET,
  output CSR_OUT,
  output [31:0] mip,
  output MEI1P,
  output MEI2P,
  output MEI3P
);

  wire _74595_1_p8, _74595_2_p11, _74595_3_p9, _74597_1_p14, _74597_2_p14, _74597_3_p14, BIT_LATCH,
       comparator_1_eq, IN_LATCH, MEI1P_IN, MEI2P_IN, MEI3P_IN, MEIP_IN, MSIP_IN, MTIP_IN, not_1_out, nPL;

  Comparator #(.Bits(12)) comparator_1 (.a(CSR_ADDR), .b(12'h344), .eq(comparator_1_eq));  // open: gt, lt
  not not_1 (not_1_out, comparator_1_eq);
  D_FF_AS d_ff_as_1 (.Set(~nRESET), .D(IN_LATCH), .C(CLK), .Clr(~1'b1), .Q(BIT_LATCH));  // open: nQ
  or or_1 (IN_LATCH, not_1_out, CSR_IN_LATCH);
  not not_2 (nPL, IN_LATCH);
  // _74595 _74595_1: pin names not known; wires that end beside it: CSR_IN, BUS_CLK, nRESET, IN_LATCH, 1'b0, 1'b1, 1'b0, _74595_1_p8
  // _74595 _74595_2: pin names not known; wires that end beside it: _74595_1_p8, BUS_CLK, nRESET, IN_LATCH, 1'b0, 1'b1, 1'b0, MEI1P_IN, MEI2P_IN, MEI3P_IN, _74595_2_p11
  // _74595 _74595_3: pin names not known; wires that end beside it: _74595_2_p11, BUS_CLK, nRESET, IN_LATCH, 1'b0, 1'b1, 1'b0, MEIP_IN, _74595_3_p9
  // _74595 _74595_4: pin names not known; wires that end beside it: _74595_3_p9, BUS_CLK, nRESET, IN_LATCH, 1'b0, 1'b1, 1'b0, MSIP_IN, MTIP_IN
  D_FF_AS d_ff_as_2 (.Set(~nINT2), .D(MEI2P_IN), .C(BIT_LATCH), .Clr(~nRESET), .Q(MEI2P));  // open: nQ
  D_FF_AS d_ff_as_3 (.Set(~nINT1), .D(MEI1P_IN), .C(BIT_LATCH), .Clr(~nRESET), .Q(MEI1P));  // open: nQ
  D_FF_AS d_ff_as_4 (.Set(~nINT3), .D(MEI3P_IN), .C(BIT_LATCH), .Clr(~nRESET), .Q(MEI3P));  // open: nQ
  // _74597 _74597_1: pin names not known; wires that end beside it: nRESET, BUS_CLK, 1'b0, CSR_OUT_LATCH, nPL, 1'b0, MEI1P, MEI2P, MEI3P, 1'b0, 1'b0, 1'b0, 1'b0, _74597_1_p14
  // _74597 _74597_2: pin names not known; wires that end beside it: nRESET, BUS_CLK, _74597_1_p14, CSR_OUT_LATCH, nPL, 1'b0, 1'b0, 1'b0, 1'b0, 1'b0, 1'b0, 1'b0, 1'b0, _74597_2_p14
  // _74597 _74597_3: pin names not known; wires that end beside it: nRESET, BUS_CLK, _74597_2_p14, CSR_OUT_LATCH, nPL, 1'b0, 1'b0, 1'b0, 1'b0, 1'b0, 1'b0, 1'b0, 1'b0, _74597_3_p14
  assign CSR_OUT = ~IN_LATCH ? _74597_3_p14 : 1'bz;  // DriverInvSel driverinvsel_1

  assign mip = {{12{1'b0}}, MEI3P, MEI2P, MEI1P, {17{1'b0}}};
endmodule
