// Digital circuit MSTATUS.dig as structural Verilog
module MSTATUS (
  input  CLK,
  input  BUS_CLK,
  input  CSR_IN,
  input  CSR_IN_LATCH,
  input  CSR_OUT_LATCH,
  input  [11:0] CSR_ADDR,
  input  IRQ,
  input  MRET,
  input  IRQ_LATCH,
  input  RESET,
  input  nRESET,
  output CSR_OUT,
  output [31:0] mstatus,
  output MIE,
  output MPIE
);

  wire _74597_1_p14, _74597_2_p14, BIT_LATCH, comparator_1_eq, d_ff_as_1_q, hef4557b_1_p15, IN_LATCH, MIE_IN,
       MIE_SET, MPIE_IN, MPIE_SET, multiplexer_1_out, multiplexer_2_out, not_1_out, nPL;

  Comparator #(.Bits(12)) comparator_1 (.a(CSR_ADDR), .b(12'h300), .eq(comparator_1_eq));  // open: gt, lt
  not not_1 (not_1_out, comparator_1_eq);
  or or_1 (IN_LATCH, not_1_out, CSR_IN_LATCH);
  not not_2 (nPL, IN_LATCH);
  D_FF_AS d_ff_as_1 (.Set(~nRESET), .D(IN_LATCH), .C(CLK), .Clr(~1'b1), .Q(d_ff_as_1_q));  // open: nQ
  and and_1 (BIT_LATCH, IRQ_LATCH, d_ff_as_1_q);
  // HEF4557B hef4557b_1: pin names not known; wires that end beside it: CSR_IN, 1'b0, 1'b1, IN_LATCH, BUS_CLK, RESET, 1'b0, 1'b1, 1'b0, 1'b1, 1'b1, 1'b1, 1'b1, 1'b0, hef4557b_1_p15
  // _74595 _74595_1: pin names not known; wires that end beside it: hef4557b_1_p15, BUS_CLK, nRESET, IN_LATCH, 1'b0, 1'b1, 1'b0, MIE_SET, MPIE_SET
  Multiplexer multiplexer_1 (.sel(MRET), .in_0(1'b0), .in_1(MPIE), .out(multiplexer_1_out));
  Multiplexer multiplexer_2 (.sel(MRET), .in_0(MIE), .in_1(MPIE), .out(multiplexer_2_out));
  D_FF_AS u_MIE (.Set(~1'b1), .D(MIE_IN), .C(BIT_LATCH), .Clr(~nRESET), .Q(MIE));  // open: nQ
  D_FF_AS u_MPIE (.Set(~1'b1), .D(MPIE_IN), .C(BIT_LATCH), .Clr(~nRESET), .Q(MPIE));  // open: nQ
  Multiplexer multiplexer_3 (.sel(IRQ), .in_0(MIE_SET), .in_1(multiplexer_1_out), .out(MIE_IN));
  Multiplexer multiplexer_4 (.sel(IRQ), .in_0(MPIE_SET), .in_1(multiplexer_2_out), .out(MPIE_IN));
  // _74597 _74597_1: pin names not known; wires that end beside it: nRESET, BUS_CLK, 1'b0, CSR_OUT_LATCH, nPL, 1'b0, 1'b0, 1'b0, 1'b1, 1'b1, 1'b0, 1'b0, 1'b0, _74597_1_p14
  // _74597 _74597_2: pin names not known; wires that end beside it: nRESET, BUS_CLK, _74597_1_p14, CSR_OUT_LATCH, nPL, 1'b0, 1'b0, 1'b0, MIE, 1'b0, 1'b0, 1'b0, MPIE, _74597_2_p14
  assign CSR_OUT = ~IN_LATCH ? _74597_2_p14 : 1'bz;  // DriverInvSel driverinvsel_1

  assign mstatus = {24'h18, MPIE, 3'b000, MIE, 3'b000};
endmodule
