// Digital circuit MTVEC.dig as structural Verilog
module MTVEC (
  input  BUS_CLK,
  input  MTVEC_SnP,
  input  CSR_IN_LATCH,
  input  [11:0] CSR_ADDR,
  input  nRESET,
  output MTVEC_OUT,
  output CSR_OUT
);

  wire and_1_out, comparator_1_eq, not_1_out, or_1_out;

  not not_1 (not_1_out, CSR_IN_LATCH);
  Comparator #(.Bits(12)) comparator_1 (.a(CSR_ADDR), .b(12'h305), .eq(comparator_1_eq));  // open: gt, lt
  and and_1 (and_1_out, not_1_out, comparator_1_eq);
  or or_1 (or_1_out, MTVEC_SnP, and_1_out);
  Imm32 mtvec (.CLK(BUS_CLK), .nRESET(nRESET), .LATCH(BUS_CLK), .SnP(or_1_out), .Val(32'h1000), .OUT(MTVEC_OUT));
  assign CSR_OUT = and_1_out ? MTVEC_OUT : 1'bz;  // Driver driver_1
endmodule
