// Digital circuit Mem-addr.dig as structural Verilog
module Mem_addr (
  input  CLK,
  input  IN,
  input  LATCH,
  input  ADDR_CLK,
  input  nPE,
  input  nRESET,
  output [31:0] ADDR
);

  wire _74161_1_p12, _74161_2_p12, _74161_3_p12, _74161_4_p12, _74161_5_p12, _74161_6_p12, _74161_7_p12,
       _74595_1_p1, _74595_1_p8, _74595_1_p9, _74595_1_p10, _74595_1_p11, _74595_1_p12, _74595_1_p13,
       _74595_1_p14, _74595_1_p15, _74595_1_p16, _74595_2_p1, _74595_2_p8, _74595_2_p9, _74595_2_p10,
       _74595_2_p11, _74595_2_p12, _74595_2_p13, _74595_2_p14, _74595_2_p15, _74595_3_p1, _74595_3_p8,
       _74595_3_p9, _74595_3_p10, _74595_3_p11, _74595_3_p12, _74595_3_p13, _74595_3_p14, _74595_3_p15,
       _74595_4_p8, _74595_4_p9, _74595_4_p10, _74595_4_p11, _74595_4_p12, _74595_4_p13, _74595_4_p14,
       _74595_4_p15;

  // _74595 _74595_1: pin names not known; wires that end beside it: _74595_1_p1, CLK, nRESET, LATCH, 1'b0, 1'b1, 1'b0, _74595_1_p8, _74595_1_p9, _74595_1_p10, _74595_1_p11, _74595_1_p12, _74595_1_p13, _74595_1_p14, _74595_1_p15, _74595_1_p16, _74595_1_p16
  // _74595 _74595_2: pin names not known; wires that end beside it: _74595_2_p1, CLK, nRESET, LATCH, 1'b0, 1'b1, 1'b0, _74595_2_p8, _74595_2_p9, _74595_2_p10, _74595_2_p11, _74595_2_p12, _74595_2_p13, _74595_2_p14, _74595_2_p15, _74595_1_p1
  // _74595 _74595_3: pin names not known; wires that end beside it: _74595_3_p1, CLK, nRESET, LATCH, 1'b0, 1'b1, 1'b0, _74595_3_p8, _74595_3_p9, _74595_3_p10, _74595_3_p11, _74595_3_p12, _74595_3_p13, _74595_3_p14, _74595_3_p15, _74595_2_p1
  // _74595 _74595_4: pin names not known; wires that end beside it: IN, CLK, nRESET, LATCH, 1'b0, 1'b1, 1'b0, _74595_4_p8, _74595_4_p9, _74595_4_p10, _74595_4_p11, _74595_4_p12, _74595_4_p13, _74595_4_p14, _74595_4_p15, _74595_3_p1
  // _74161 _74161_1: pin names not known; wires that end beside it: nPE, nRESET, ADDR_CLK, 1'b1, 1'b1, _74595_1_p8, _74595_1_p9, _74595_1_p10, _74595_1_p11, 1'b1, 1'b0, _74161_1_p12, ADDR[0], ADDR[1], ADDR[2], ADDR[3]
  // _74161 _74161_2: pin names not known; wires that end beside it: nPE, nRESET, ADDR_CLK, _74161_1_p12, 1'b1, _74595_1_p12, _74595_1_p13, _74595_1_p14, _74595_1_p15, 1'b1, 1'b0, _74161_2_p12, ADDR[4], ADDR[5], ADDR[6], ADDR[7]
  // _74161 _74161_3: pin names not known; wires that end beside it: nPE, nRESET, ADDR_CLK, _74161_2_p12, 1'b1, _74595_2_p8, _74595_2_p9, _74595_2_p10, _74595_2_p11, 1'b1, 1'b0, _74161_3_p12, ADDR[8], ADDR[9], ADDR[10], ADDR[11]
  // _74161 _74161_4: pin names not known; wires that end beside it: nPE, nRESET, ADDR_CLK, _74161_3_p12, 1'b1, _74595_2_p12, _74595_2_p13, _74595_2_p14, _74595_2_p15, 1'b1, 1'b0, _74161_4_p12, ADDR[12], ADDR[13], ADDR[14], ADDR[15]
  // _74161 _74161_5: pin names not known; wires that end beside it: nPE, nRESET, ADDR_CLK, _74161_4_p12, 1'b1, _74595_3_p8, _74595_3_p9, _74595_3_p10, _74595_3_p11, 1'b1, 1'b0, _74161_5_p12, ADDR[16], ADDR[17], ADDR[18], ADDR[19]
  // _74161 _74161_6: pin names not known; wires that end beside it: nPE, nRESET, ADDR_CLK, _74161_5_p12, 1'b1, _74595_3_p12, _74595_3_p13, _74595_3_p14, _74595_3_p15, 1'b1, 1'b0, _74161_6_p12, ADDR[20], ADDR[21], ADDR[22], ADDR[23]
  // _74161 _74161_7: pin names not known; wires that end beside it: nPE, nRESET, ADDR_CLK, _74161_6_p12, 1'b1, _74595_4_p8, _74595_4_p9, _74595_4_p10, _74595_4_p11, 1'b1, 1'b0, _74161_7_p12, ADDR[24], ADDR[25], ADDR[26], ADDR[27]
  // _74161 _74161_8: pin names not known; wires that end beside it: nPE, nRESET, ADDR_CLK, _74161_7_p12, 1'b1, _74595_4_p12, _74595_4_p13, _74595_4_p14, _74595_4_p15, 1'b1, 1'b0, ADDR[28], ADDR[29], ADDR[30], ADDR[31]
endmodule

/* Test case:
CLK IN          LATCH ADDR-CLK ~PE ~RESET   ADDR

loop (rep,32)

let addr = random(1<<32);

0   0           0     0        1   0        0

loop (i,32)
0   (addr>>i&1) 0     0        0   1        X
1   (addr>>i&1) 0     0        0   1        X
end loop
0   0           1     0        0   1        0
0   0           1     1        0   1        (addr)
0   0           0     0        1   1        X
0   0           0     1        1   1        (addr+1)
0   0           0     0        1   1        X
0   0           0     1        1   1        (addr+2)
0   0           0     0        1   1        X
0   0           0     1        1   1        (addr+3)

end loop
*/
