// Digital circuit Mem-decode.dig as structural Verilog
module Mem_decode (
  input  [31:0] ADDR,
  input  [7:0] IN,
  input  nOE,
  input  nWE,
  input  [7:0] ROM_DATA,
  output [7:0] OUT,
  output [15:0] ROM_ADDR,
  output ROM_SEL,
  output nKB_INT
);

  wire and_1_out, and_2_out, comparator_1_eq, comparator_2_eq, demultiplexer_1_out_0, demultiplexer_1_out_2,
       demultiplexer_1_out_3, keyboard_1_av, nand_1_out, or_1_out;
  wire [7:0] keyboard_1_d;
  wire [15:8] keyboard_1_d_2;

  assign OUT = ~nWE ? IN : 8'bz;  // DriverInvSel driverinvsel_1
  Demultiplexer #(.Selector_Bits(2), .Default(1)) demultiplexer_1 (
    .sel(ADDR[31:30]), .in(1'b0), .out_0(demultiplexer_1_out_0), .out_2(demultiplexer_1_out_2),
    .out_3(demultiplexer_1_out_3));  // open: out_1
  Comparator #(.Bits(16)) comparator_1 (.a(ADDR[15:0]), .b({16{1'b0}}), .eq(comparator_1_eq));  // open: gt, lt
  Comparator #(.Bits(16)) comparator_2 (.a(ADDR[15:0]), .b(16'h1), .eq(comparator_2_eq));  // open: gt, lt
  and and_1 (and_1_out, ~demultiplexer_1_out_3, comparator_1_eq);  // And
  and and_2 (and_2_out, ~demultiplexer_1_out_3, comparator_2_eq);  // And
  RAMSinglePortSel #(.AddrBits(16), .Bits(8)) RAM (
    .A(ADDR[15:0]), .CS(~demultiplexer_1_out_2), .WE(~nWE), .OE(~nOE), .D(OUT));
  nand nand_1 (nand_1_out, ~nOE, and_2_out);  // NAnd
  not not_1 (ROM_SEL, demultiplexer_1_out_0);
  or or_1 (or_1_out, demultiplexer_1_out_0, nOE);
  Terminal terminal_1 (.D(OUT), .C(nWE), .en(and_1_out));
  Keyboard keyboard_1 (.C(nOE), .en(and_2_out), .D({keyboard_1_d_2, keyboard_1_d}), .av(keyboard_1_av));
  assign OUT = ~or_1_out ? ROM_DATA : 8'bz;  // DriverInvSel driverinvsel_2
  assign OUT = ~nand_1_out ? keyboard_1_d : 8'bz;  // DriverInvSel driverinvsel_3
  not not_2 (nKB_INT, keyboard_1_av);

  assign ROM_ADDR = ADDR[15:0];
endmodule

/* Test case:
ADDR       ~OE ~WE IN          OUT

0x00000000 1   1   Z           Z
0x00000000 0   1   Z           0x00
0x00000010 0   1   Z           0x10
0x000000AA 0   1   Z           0xAA
0x0000001F 0   1   Z           0x1F

0x80000000 1   0   0xDE        X
0x80000010 1   0   0xAD        X
0x80000000 0   1   Z           0xDE
0x80000010 0   1   Z           0xAD
0x4000001F 0   1   Z           Z
*/
