// Digital circuit OpCode.dig as structural Verilog
module OpCode (
  input  CLK,
  input  IN,
  input  LATCH_OP,
  input  LATCH_IMM,
  input  SnP_IMM,
  input  nRESET,
  output ImmI,
  output ImmS,
  output ImmB,
  output ImmU,
  output ImmJ,
  output Const1,
  output Const31,
  output ImmCSR,
  output [3:0] RSA,
  output [3:0] RSB,
  output [3:0] RSD,
  output [4:0] OPCODE,
  output [2:0] FUNC3,
  output SA_ALU,
  output nS_EXT,
  output SYS,
  output [1:0] TRAP2,
  output [31:0] Instr,
  output [15:0] DImmI
);

  wire _74hc595_2_qh_2, _74hc595_3_qh_2, _74hc595_4_qh_2;

  _74HC595 _74hc595_1 (
    .SER(_74hc595_2_qh_2), .SRCLK(CLK), .nSRCLR(nRESET), .RCLK(LATCH_OP), .nOE(1'b0), .VCC(1'b1), .GND(1'b0),
    .QH(Instr[0]), .QG(Instr[1]), .QF(Instr[2]), .QE(Instr[3]), .QD(Instr[4]), .QC(Instr[5]), .QB(Instr[6]),
    .QA(Instr[7]));  // open: QH_2
  _74HC595 _74hc595_2 (
    .SER(_74hc595_3_qh_2), .SRCLK(CLK), .nSRCLR(nRESET), .RCLK(LATCH_OP), .nOE(1'b0), .VCC(1'b1), .GND(1'b0),
    .QH(Instr[8]), .QG(Instr[9]), .QF(Instr[10]), .QE(Instr[11]), .QD(FUNC3[0]), .QC(FUNC3[1]),
    .QB(FUNC3[2]), .QA(Instr[15]), .QH_2(_74hc595_2_qh_2));
  _74HC595 _74hc595_3 (
    .SER(_74hc595_4_qh_2), .SRCLK(CLK), .nSRCLR(nRESET), .RCLK(LATCH_OP), .nOE(1'b0), .VCC(1'b1), .GND(1'b0),
    .QH(Instr[16]), .QG(Instr[17]), .QF(Instr[18]), .QE(Instr[19]), .QD(Instr[20]), .QC(Instr[21]),
    .QB(Instr[22]), .QA(Instr[23]), .QH_2(_74hc595_3_qh_2));
  _74HC595 _74hc595_4 (
    .SER(IN), .SRCLK(CLK), .nSRCLR(nRESET), .RCLK(LATCH_OP), .nOE(1'b0), .VCC(1'b1), .GND(1'b0),
    .QH(Instr[24]), .QG(Instr[25]), .QF(Instr[26]), .QE(Instr[27]), .QD(Instr[28]), .QC(Instr[29]),
    .QB(Instr[30]), .QA(Instr[31]), .QH_2(_74hc595_4_qh_2));
  Imm16 u_ImmI (
    .CLK(CLK), .nRESET(nRESET), .LATCH(LATCH_IMM), .SnP(SnP_IMM), .Val({{5{Instr[31]}}, Instr[30:20]}),
    .OUT(ImmI), .DVal(DImmI));
  Imm16 u_ImmS (
    .CLK(CLK), .nRESET(nRESET), .LATCH(LATCH_IMM), .SnP(SnP_IMM),
    .Val({{5{Instr[31]}}, Instr[30:25], Instr[11:7]}), .OUT(ImmS));  // open: DVal
  Imm16 u_ImmB (
    .CLK(CLK), .nRESET(nRESET), .LATCH(LATCH_IMM), .SnP(SnP_IMM),
    .Val({{4{Instr[31]}}, Instr[7], Instr[30:25], Instr[11:8], 1'b0}), .OUT(ImmB));  // open: DVal
  Imm32 u_ImmU (
    .CLK(CLK), .nRESET(nRESET), .LATCH(LATCH_IMM), .SnP(SnP_IMM), .Val({Instr[31:15], FUNC3, {12{1'b0}}}),
    .OUT(ImmU));
  Imm24 u_ImmJ (
    .CLK(CLK), .nRESET(nRESET), .LATCH(LATCH_IMM), .SnP(SnP_IMM),
    .Val({{5{Instr[31]}}, Instr[19:15], FUNC3, Instr[30:21], 1'b0}), .OUT(ImmJ));
  Imm8 u_Const31 (.CLK(CLK), .nRESET(nRESET), .LATCH(LATCH_IMM), .SnP(SnP_IMM), .Val(8'h1f), .OUT(Const31));
  Imm8 u_ImmCSR (
    .CLK(CLK), .nRESET(nRESET), .LATCH(LATCH_IMM), .SnP(SnP_IMM), .Val({3'b000, Instr[19:15]}), .OUT(ImmCSR));
  or or_1 (SA_ALU, Instr[30], Instr[29]);
  Imm8 u_Const1 (.CLK(CLK), .nRESET(nRESET), .LATCH(LATCH_IMM), .SnP(SnP_IMM), .Val(8'h1), .OUT(Const1));

  assign Instr[14:12] = FUNC3;
  assign nS_EXT = FUNC3[2];
  assign OPCODE = Instr[6:2];
  assign RSA = Instr[18:15];
  assign RSB = Instr[23:20];
  assign RSD = Instr[10:7];
  assign SYS = Instr[28];
  assign TRAP2 = Instr[21:20];

  // Other names for the same wires on the sheet: B0 = Instr[0]; B1 = Instr[1]; B2 = Instr[2]; B3 = Instr[3];
  //   B4 = Instr[4]; B5 = Instr[5]; B6 = Instr[6]; B7 = Instr[7]; B8 = Instr[8]; B9 = Instr[9]; B10 = Instr[10];
  //   B11 = Instr[11]; B12 = FUNC3[0]; B13 = FUNC3[1]; B14 = FUNC3[2]; B15 = Instr[15]; B16 = Instr[16];
  //   B17 = Instr[17]; B18 = Instr[18]; B19 = Instr[19]; B20 = Instr[20]; B21 = Instr[21]; B22 = Instr[22];
  //   B23 = Instr[23]; B24 = Instr[24]; B25 = Instr[25]; B26 = Instr[26]; B27 = Instr[27]; B28 = Instr[28];
  //   B29 = Instr[29]; B30 = Instr[30]; B31 = Instr[31]; LATCH_IM = LATCH_IMM; SP_IMM = SnP_IMM
endmodule

/* Test case ADD/ADDI/BEQ:
CLK IN           ~RESET LATCH_OP LATCH_IMM S~P_IMM     ImmI        ImmB        RSA   RSB   RSD   FUNC3   OPCODE  SA_ALU

loop (rep, 32)

# Bin immediate

let imm = random(1<<12);
let s = (imm >> 11) & 1;
let op = 0b00100;
let func3 = random(8);
let rd = random(16);
let rs1 = random(16);

let instr = ((imm << 20) | (rs1 << 15) | (func3 << 12) | (rd << 7) | (op << 2) | 0b11) & 0xFFFFFFFF;

0   0            0      0        0         1           X           X           X     X     X     X       X       X

loop (i,32)
0   (instr>>i&1) 1      0        0         0           X           X           X     X     X     X       X       X
1   (instr>>i&1) 1      0        0         0           X           X           X     X     X     X       X       X
end loop

0   0            1      1        0         0           X           X           X     X     X     X       X       X
1   0            1      1        0         0           X           X           X     X     X     X       X       X

0   0            1      0        1         0           X           X           X     X     X     X       X       X
1   0            1      0        1         0           X           X           (rs1) X     (rd)  (func3) (op)    X

loop (i,12)
0   0            1      0        0         1           (imm>>i&1)  X           X     X     X     X       X       X
1   0            1      0        0         1           X           X           X     X     X     X       X       X
end loop

loop (i,20)
0   0            1      0        0         1           (s)         X           X     X     X     X       X       X
1   0            1      0        0         1           X           X           X     X     X     X       X       X
end loop


# SUB

let s = (imm >> 11) & 1;
let op = 0b01100;
let func3 = 000;
let rd = random(16);
let rs1 = random(16);
let rs2 = random(16);

let instr = ((0b0100000 << 25) | (rs2 << 20) | (rs1 << 15) | (func3 << 12) | (rd << 7) | (op << 2) | 0b11) & 0xFFFFFFFF;

0   0            0      0        0         1           X           X           X     X     X     X       X       X

loop (i,32)
0   (instr>>i&1) 1      0        0         0           X           X           X     X     X     X       X       X
1   (instr>>i&1) 1      0        0         0           X           X           X     X     X     X       X       X
end loop

0   0            1      1        0         0           X           X           X     X     X     X       X       X
1   0            1      1        0         0           X           X           X     X     X     X       X       X

0   0            1      0        1         0           X           X           X     X     X     X       X       X
1   0            1      0        1         0           X           X           (rs1) (rs2) (rd)  (func3) (op)    1

# BEQ

let imm12 = random(1<<1);
let imm10to5 = random(1<<6);
let imm4to1 = random(1<<4);
let imm11 = random(1<<1);
let rs1 = random(1<<4);
let rs2 = random(1<<4);
let funct3 = 0;
let op = 0b11000;

let imm = (imm12 << 12) | (imm11 << 11) | (imm10to5 << 5) | (imm4to1 << 1);
let s = (imm >> 12) & 1;

let instr = (imm12 << 31) | (imm10to5 << 25) | (rs2 << 20) | (rs1 << 15) | (funct3 << 12) | (imm4to1 << 8) | (imm11 << 7) | (op << 2) | (0b11);

0   0            0      0        0         1           X           X           X     X     X     X       X       X

loop (i,32)
0   (instr>>i&1) 1      0        0         0           X           X           X     X     X     X       X       X
1   (instr>>i&1) 1      0        0         0           X           X           X     X     X     X       X       X
end loop

0   0            1      1        0         0           X           X           X     X     X     X       X       X
1   0            1      1        0         0           X           X           X     X     X     X       X       X

0   0            1      0        1         0           X           X           X     X     X     X       X       X
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*/
