// Digital circuit PC.dig as structural Verilog
module PC (
  input  nRESET,
  input  nLD_PC,
  input  CLK,
  input  LATCH_OUT,
  input  nPL_OUT,
  input  IN,
  input  LATCH_IN,
  input  CNT_EN,
  output OUT,
  output D
);

  wire _74hc595_1_qa, _74hc595_1_qb, _74hc595_1_qc, _74hc595_1_qd, _74hc595_1_qe, _74hc595_1_qf,
       _74hc595_1_qg, _74hc595_2_qa, _74hc595_2_qb, _74hc595_2_qc, _74hc595_2_qd, _74hc595_2_qe,
       _74hc595_2_qf, _74hc595_2_qg, _74hc595_2_qh, _74hc595_2_qh_2, _74hc595_3_qa, _74hc595_3_qb,
       _74hc595_3_qc, _74hc595_3_qd, _74hc595_3_qe, _74hc595_3_qf, _74hc595_3_qg, _74hc595_3_qh,
       _74hc595_3_qh_2, _74hc595_4_qa, _74hc595_4_qb, _74hc595_4_qc, _74hc595_4_qd, _74hc595_4_qe,
       _74hc595_4_qf, _74hc595_4_qg, _74hc595_4_qh, _74hc595_4_qh_2, _74hc597_2_q7, _74hc597_3_q7,
       _74hc597_4_q7, _74161_1_p12, _74161_1_p13, _74161_1_p14, _74161_1_p15, _74161_1_p16, _74161_2_p12,
       _74161_2_p13, _74161_2_p14, _74161_2_p15, _74161_2_p16, _74161_3_p12, _74161_3_p13, _74161_3_p14,
       _74161_3_p15, _74161_3_p16, _74161_4_p12, _74161_4_p13, _74161_4_p14, _74161_4_p15, _74161_4_p16,
       _74161_5_p12, _74161_5_p13, _74161_5_p14, _74161_5_p15, _74161_5_p16, _74161_6_p12, _74161_6_p13,
       _74161_6_p14, _74161_6_p15, _74161_6_p16, _74161_7_p12, _74161_7_p13, _74161_7_p14, _74161_7_p15,
       _74161_7_p16, _74161_8_p12, _74161_8_p13, or_1_out;

  _74HC595 _74hc595_1 (
    .SER(_74hc595_2_qh_2), .SRCLK(CLK), .nSRCLR(nRESET), .RCLK(LATCH_IN), .nOE(1'b0), .VCC(1'b1), .GND(1'b0),
    .QG(_74hc595_1_qg), .QF(_74hc595_1_qf), .QE(_74hc595_1_qe), .QD(_74hc595_1_qd), .QC(_74hc595_1_qc),
    .QB(_74hc595_1_qb), .QA(_74hc595_1_qa));  // open: QH, QH_2
  _74HC595 _74hc595_2 (
    .SER(_74hc595_3_qh_2), .SRCLK(CLK), .nSRCLR(nRESET), .RCLK(LATCH_IN), .nOE(1'b0), .VCC(1'b1), .GND(1'b0),
    .QH(_74hc595_2_qh), .QG(_74hc595_2_qg), .QF(_74hc595_2_qf), .QE(_74hc595_2_qe), .QD(_74hc595_2_qd),
    .QC(_74hc595_2_qc), .QB(_74hc595_2_qb), .QA(_74hc595_2_qa), .QH_2(_74hc595_2_qh_2));
  _74HC595 _74hc595_3 (
    .SER(_74hc595_4_qh_2), .SRCLK(CLK), .nSRCLR(nRESET), .RCLK(LATCH_IN), .nOE(1'b0), .VCC(1'b1), .GND(1'b0),
    .QH(_74hc595_3_qh), .QG(_74hc595_3_qg), .QF(_74hc595_3_qf), .QE(_74hc595_3_qe), .QD(_74hc595_3_qd),
    .QC(_74hc595_3_qc), .QB(_74hc595_3_qb), .QA(_74hc595_3_qa), .QH_2(_74hc595_3_qh_2));
  _74HC595 _74hc595_4 (
    .SER(IN), .SRCLK(CLK), .nSRCLR(nRESET), .RCLK(LATCH_IN), .nOE(1'b0), .VCC(1'b1), .GND(1'b0),
    .QH(_74hc595_4_qh), .QG(_74hc595_4_qg), .QF(_74hc595_4_qf), .QE(_74hc595_4_qe), .QD(_74hc595_4_qd),
    .QC(_74hc595_4_qc), .QB(_74hc595_4_qb), .QA(_74hc595_4_qa), .QH_2(_74hc595_4_qh_2));
  or or_1 (or_1_out, CLK, nLD_PC);
  D_FF_AS d_ff_as_1 (.Set(1'b0), .D(_74hc595_1_qg), .C(or_1_out), .Clr(~nRESET), .Q(D));  // open: nQ
  // _74161 _74161_1: pin names not known; wires that end beside it: nLD_PC, nRESET, CLK, 1'b1, CNT_EN, _74hc595_1_qf, _74hc595_1_qe, _74hc595_1_qd, _74hc595_1_qc, 1'b1, 1'b0, _74161_1_p12, _74161_1_p13, _74161_1_p14, _74161_1_p15, _74161_1_p16
  // _74161 _74161_2: pin names not known; wires that end beside it: nLD_PC, nRESET, CLK, _74161_1_p12, CNT_EN, _74hc595_1_qb, _74hc595_1_qa, _74hc595_2_qh, _74hc595_2_qg, 1'b1, 1'b0, _74161_2_p12, _74161_2_p13, _74161_2_p14, _74161_2_p15, _74161_2_p16
  // _74161 _74161_3: pin names not known; wires that end beside it: nLD_PC, nRESET, CLK, _74161_2_p12, CNT_EN, _74hc595_2_qf, _74hc595_2_qe, _74hc595_2_qd, _74hc595_2_qc, 1'b1, 1'b0, _74161_3_p12, _74161_3_p13, _74161_3_p14, _74161_3_p15, _74161_3_p16
  // _74161 _74161_4: pin names not known; wires that end beside it: nLD_PC, nRESET, CLK, _74161_3_p12, CNT_EN, _74hc595_2_qb, _74hc595_2_qa, _74hc595_3_qh, _74hc595_3_qg, 1'b1, 1'b0, _74161_4_p12, _74161_4_p13, _74161_4_p14, _74161_4_p15, _74161_4_p16
  // _74161 _74161_5: pin names not known; wires that end beside it: nLD_PC, nRESET, CLK, _74161_4_p12, CNT_EN, _74hc595_3_qf, _74hc595_3_qe, _74hc595_3_qd, _74hc595_3_qc, 1'b1, 1'b0, _74161_5_p12, _74161_5_p13, _74161_5_p14, _74161_5_p15, _74161_5_p16
  // _74161 _74161_6: pin names not known; wires that end beside it: nLD_PC, nRESET, CLK, _74161_5_p12, CNT_EN, _74hc595_3_qb, _74hc595_3_qa, _74hc595_4_qh, _74hc595_4_qg, 1'b1, 1'b0, _74161_6_p12, _74161_6_p13, _74161_6_p14, _74161_6_p15, _74161_6_p16
  // _74161 _74161_7: pin names not known; wires that end beside it: nLD_PC, nRESET, CLK, _74161_6_p12, CNT_EN, _74hc595_4_qf, _74hc595_4_qe, _74hc595_4_qd, _74hc595_4_qc, 1'b1, 1'b0, _74161_7_p12, _74161_7_p13, _74161_7_p14, _74161_7_p15, _74161_7_p16
  // _74161 _74161_8: pin names not known; wires that end beside it: nLD_PC, nRESET, CLK, _74161_7_p12, CNT_EN, _74hc595_4_qb, _74hc595_4_qa, 1'b0, 1'b0, 1'b1, 1'b0, _74161_8_p12, _74161_8_p13
  _74HC597 _74hc597_1 (
    .nMR(nRESET), .SHCP(CLK), .DS(_74hc597_2_q7), .STCP(LATCH_OUT), .nPL(nPL_OUT), .D7(1'b0), .D6(D),
    .D5(_74161_1_p13), .D4(_74161_1_p14), .D3(_74161_1_p15), .D2(_74161_1_p16), .D1(_74161_2_p13),
    .D0(_74161_2_p14), .Q7(OUT));
  _74HC597 _74hc597_2 (
    .nMR(nRESET), .SHCP(CLK), .DS(_74hc597_3_q7), .STCP(LATCH_OUT), .nPL(nPL_OUT), .D7(_74161_2_p15),
    .D6(_74161_2_p16), .D5(_74161_3_p13), .D4(_74161_3_p14), .D3(_74161_3_p15), .D2(_74161_3_p16),
    .D1(_74161_4_p13), .D0(_74161_4_p14), .Q7(_74hc597_2_q7));
  _74HC597 _74hc597_3 (
    .nMR(nRESET), .SHCP(CLK), .DS(_74hc597_4_q7), .STCP(LATCH_OUT), .nPL(nPL_OUT), .D7(_74161_4_p15),
    .D6(_74161_4_p16), .D5(_74161_5_p13), .D4(_74161_5_p14), .D3(_74161_5_p15), .D2(_74161_5_p16),
    .D1(_74161_6_p13), .D0(_74161_6_p14), .Q7(_74hc597_3_q7));
  _74HC597 _74hc597_4 (
    .nMR(nRESET), .SHCP(CLK), .DS(1'b0), .STCP(LATCH_OUT), .nPL(nPL_OUT), .D7(_74161_6_p15),
    .D6(_74161_6_p16), .D5(_74161_7_p13), .D4(_74161_7_p14), .D3(_74161_7_p15), .D2(_74161_7_p16),
    .D1(_74161_8_p12), .D0(_74161_8_p13), .Q7(_74hc597_4_q7));
endmodule

/* Test case:
CLK IN         LATCH_IN LATCH_OUT ~PL_OUT CNT_EN ~LD_PC ~RESET   D OUT

loop (rep, 32)

let PC = random(1<<31) << 1;

0   0          0        0         0       0      1       0       X X

loop (i,32)
0   (PC>>i&1)  0        0         0       0      1       1       X X
1   (PC>>i&1)  0        0         0       0      1       1       X X
end loop

0   0          1        0         0       1      0       1       X X
1   0          1        0         0       1      0       1       X X

0   0          0        1         0       0      1       1       X X
1   0          0        1         0       0      1       1       X X

loop (i,32)
0   0          0        0         1       0      1       1       X  (PC>>i&1)
1   0          0        0         1       0      1       1       X X
end loop

end loop
*/
