// Digital circuit Register-bank-8.dig as structural Verilog
module Register_bank_8 (
  input  CLK,
  input  IN,
  input  nEN_IN,
  input  nEN,
  input  [2:0] SA,
  input  [2:0] SB,
  input  [2:0] SD,
  input  RESET,
  output A,
  output B
);

  wire demultiplexer_1_out_0, demultiplexer_1_out_1, demultiplexer_1_out_2, demultiplexer_1_out_3,
       demultiplexer_1_out_4, demultiplexer_1_out_5, demultiplexer_1_out_6, demultiplexer_1_out_7,
       register_1_out, register_2_out, register_3_out, register_4_out, register_5_out, register_6_out,
       register_7_out, register_8_out;

  Demultiplexer #(.Selector_Bits(3), .Default(1)) demultiplexer_1 (
    .sel(SD), .in(nEN_IN), .out_0(demultiplexer_1_out_0), .out_1(demultiplexer_1_out_1),
    .out_2(demultiplexer_1_out_2), .out_3(demultiplexer_1_out_3), .out_4(demultiplexer_1_out_4),
    .out_5(demultiplexer_1_out_5), .out_6(demultiplexer_1_out_6), .out_7(demultiplexer_1_out_7));
  Register register_1 (
    .CLK(CLK), .IN(IN), .nEN_IN(demultiplexer_1_out_0), .nEN(nEN), .RESET(RESET), .OUT(register_1_out));
  Register register_2 (
    .CLK(CLK), .IN(IN), .nEN_IN(demultiplexer_1_out_1), .nEN(nEN), .RESET(RESET), .OUT(register_2_out));
  Register register_3 (
    .CLK(CLK), .IN(IN), .nEN_IN(demultiplexer_1_out_2), .nEN(nEN), .RESET(RESET), .OUT(register_3_out));
  Register register_4 (
    .CLK(CLK), .IN(IN), .nEN_IN(demultiplexer_1_out_3), .nEN(nEN), .RESET(RESET), .OUT(register_4_out));
  Register register_5 (
    .CLK(CLK), .IN(IN), .nEN_IN(demultiplexer_1_out_4), .nEN(nEN), .RESET(RESET), .OUT(register_5_out));
  Register register_6 (
    .CLK(CLK), .IN(IN), .nEN_IN(demultiplexer_1_out_5), .nEN(nEN), .RESET(RESET), .OUT(register_6_out));
  Register register_7 (
    .CLK(CLK), .IN(IN), .nEN_IN(demultiplexer_1_out_6), .nEN(nEN), .RESET(RESET), .OUT(register_7_out));
  Register register_8 (
    .CLK(CLK), .IN(IN), .nEN_IN(demultiplexer_1_out_7), .nEN(nEN), .RESET(RESET), .OUT(register_8_out));
  Multiplexer #(.Selector_Bits(3)) multiplexer_1 (
    .sel(SA), .in_0(register_1_out), .in_1(register_2_out), .in_2(register_3_out), .in_3(register_4_out),
    .in_4(register_5_out), .in_5(register_6_out), .in_6(register_7_out), .in_7(register_8_out), .out(A));
  Multiplexer #(.Selector_Bits(3)) multiplexer_2 (
    .sel(SB), .in_0(register_1_out), .in_1(register_2_out), .in_2(register_3_out), .in_3(register_4_out),
    .in_4(register_5_out), .in_5(register_6_out), .in_6(register_7_out), .in_7(register_8_out), .out(B));
endmodule
