// Digital circuit Register-bank.dig as structural Verilog
module Register_bank (
  input  CLK,
  input  IN,
  input  nEN,
  input  nEN_IN,
  input  [3:0] SA,
  input  [3:0] SB,
  input  [3:0] SD,
  input  RESET,
  output A,
  output B
);

  wire demultiplexer_1_out_0, demultiplexer_1_out_1, register_bank_0_1_a, register_bank_0_1_b,
       register_bank_8_1_a, register_bank_8_1_b;

  Demultiplexer #(.Default(1)) demultiplexer_1 (
    .sel(SD[3]), .in(nEN_IN), .out_0(demultiplexer_1_out_0), .out_1(demultiplexer_1_out_1));
  Register_bank_0 register_bank_0_1 (
    .CLK(CLK), .IN(IN), .nEN_IN(demultiplexer_1_out_0), .nEN(nEN), .SA(SA[2:0]), .SB(SB[2:0]), .SD(SD[2:0]),
    .RESET(RESET), .A(register_bank_0_1_a), .B(register_bank_0_1_b));
  Register_bank_8 register_bank_8_1 (
    .CLK(CLK), .IN(IN), .nEN_IN(demultiplexer_1_out_1), .nEN(nEN), .SA(SA[2:0]), .SB(SB[2:0]), .SD(SD[2:0]),
    .RESET(RESET), .A(register_bank_8_1_a), .B(register_bank_8_1_b));
  Multiplexer multiplexer_1 (.sel(SA[3]), .in_0(register_bank_0_1_a), .in_1(register_bank_8_1_a), .out(A));
  Multiplexer multiplexer_2 (.sel(SB[3]), .in_0(register_bank_0_1_b), .in_1(register_bank_8_1_b), .out(B));

  // Other names for the same wires on the sheet: SA012[2:0] = SA[2:0]; SB012[2:0] = SB[2:0]; SD012[2:0] = SD[2:0]
endmodule

/* Test case:
CLK IN        ~EN ~EN_IN RESET SA   SB   SD     A        B

loop (rep,32)

let R1 = 1 + random(14);
let R2 = 1 + R1 + random(15-R1);

let A = random(1<<32);
let B = random(1<<32);


0   0         1   1      1     0    0    0      0        0

loop (i,32)
0   (A>>i&1)  0   0      0     0    0    (R1)   0        0
1   (A>>i&1)  0   0      0     0    0    (R1)   X        X
end loop

loop (i,32)
0   (B>>i&1)  0   0      0     (R1) 0    (R2)   (A>>i&1) 0
1   (B>>i&1)  0   0      0     (R1) 0    (R2)   X        X
end loop

loop (i,32)
0   0         0   1      0     (R1) (R2) 0      (A>>i&1) (B>>i&1)
1   0         0   1      0     (R1) (R2) 0      X        X
end loop

loop (i,32)
0   0         0   1      0     (R2) (R1) 0      (B>>i&1) (A>>i&1)
1   0         0   1      0     (R2) (R1) 0      X        X
end loop


loop (i,32)
0   0         0   1      0     (R2) (R2) 0      (B>>i&1) (B>>i&1)
1   0         0   1      0     (R2) (R2) 0      X        X
end loop

end loop
*/
