// Digital circuit Register.dig as structural Verilog
module Register (
  input  CLK,
  input  IN,
  input  nIN_EN,
  input  nEN,
  input  RESET,
  output OUT
);

  // HEF4557B hef4557b_1: pin names not known; wires that end beside it: OUT, IN, nIN_EN, nEN, CLK, RESET, 1'b0, 1'b1, 1'b1, 1'b1, 1'b1, 1'b1, 1'b1, 1'b0, OUT

  // Notes on the sheet:
  //   CLK: Hz: 4
endmodule
