// Digital circuit SD-SPI.dig as structural Verilog
module SD_SPI (
  input  clk,
  input  nWE,
  input  [7:0] in_7,
  input  nOE,
  input  nRD_WR,
  output [7:0] out_1,
  output [3:0] out_4,
  output [3:0] out_5,
  output nWAIT,
  output [7:0] out_8,
  output [7:0] out_10
);

  wire _74hc597_1_q7, _74hc597_2_q7, and_1_out, d_ff_as_2_q, nand_2_out, nOE_t, not_2_out, nSPI_CLK, nSPI_EN,
       nTRIG, nWE_t, or_3_out, reset_1_out, reset_2_out, reset_3_out, reset_4_out, reset_5_out, SPI_CLK,
       SPI_EN;

  nand nand_1 (nWAIT, nand_2_out, SPI_EN);
  nand nand_2 (nand_2_out, nOE, nWE);
  or or_1 (nWE_t, nWE, SPI_EN);
  or or_2 (nOE_t, nOE, SPI_EN);
  or or_3 (or_3_out, nRD_WR, nOE_t);
  Reset reset_1 (.out(reset_1_out));
  and and_1 (and_1_out, nTRIG, _74hc597_1_q7);
  and and_2 (nTRIG, or_3_out, nWE_t);
  D_FF_AS d_ff_as_1 (.Set(~1'b1), .D(and_1_out), .C(clk), .Clr(~reset_1_out), .Q(SPI_EN), .nQ(nSPI_EN));
  or or_4 (nSPI_CLK, clk, nSPI_EN);
  Counter #(.Bits(4)) counter_1 (.en(1'b1), .C(nSPI_CLK), .clr(reset_2_out), .out(out_5));  // open: ovf
  Reset #(.invertOutput("false")) reset_2 (.out(reset_2_out));
  not not_1 (SPI_CLK, nSPI_CLK);
  Counter #(.Bits(4)) counter_2 (.en(1'b1), .C(SPI_CLK), .clr(reset_2_out), .out(out_4));  // open: ovf
  Reset reset_3 (.out(reset_3_out));
  _74HC597 _74hc597_1 (
    .nMR(reset_3_out), .SHCP(SPI_CLK), .DS(1'b0), .STCP(reset_3_out), .nPL(nTRIG), .D7(1'b1), .D6(1'b1),
    .D5(1'b1), .D4(1'b1), .D3(1'b1), .D2(1'b1), .D1(1'b1), .D0(1'b1), .Q7(_74hc597_1_q7), .Val(out_1));
  D_FF_AS d_ff_as_2 (.Set(1'b0), .D(1'b1), .C(SPI_EN), .Clr(~nWE_t), .Q(d_ff_as_2_q));  // open: nQ
  Reset reset_4 (.out(reset_4_out));
  Reset reset_5 (.out(reset_5_out));
  not not_2 (not_2_out, nOE_t);
  _74HC597 _74hc597_2 (
    .nMR(reset_5_out), .SHCP(nSPI_CLK), .DS(1'b1), .STCP(nWE_t), .nPL(d_ff_as_2_q), .D7(in_7[0]),
    .D6(in_7[1]), .D5(in_7[2]), .D4(in_7[3]), .D3(in_7[4]), .D2(in_7[5]), .D1(in_7[6]), .D0(in_7[7]),
    .Q7(_74hc597_2_q7), .Val(out_8));
  _74HC595 _74hc595_1 (
    .SER(_74hc597_2_q7), .SRCLK(SPI_CLK), .nSRCLR(reset_4_out), .RCLK(not_2_out), .nOE(nOE_t), .VCC(1'b1),
    .GND(1'b0), .QH(out_10[0]), .QG(out_10[1]), .QF(out_10[2]), .QE(out_10[3]), .QD(out_10[4]),
    .QC(out_10[5]), .QB(out_10[6]), .QA(out_10[7]));  // open: QH_2

  // Notes on the sheet:
  //   nWE: default 1
  //   in_7: default 170
  //   nOE: default 1
  //   nRD_WR: default 1
endmodule
