// Digital circuit Substep-Counter.dig as structural Verilog
module Substep_Counter (
  input  nCLK,
  input  nRESET,
  input  CLK,
  input  [1:0] LEN,
  output LAST,
  output nDONE,
  output [7:0] DVAL,
  output DONE
);

  wire _74161_1_pin15, and_1_out, and_2_out, not_1_out, switchdt_1_p3;

  not not_1 (not_1_out, CLK);
  // SwitchDT switchdt_1: pin names not known; wires that end beside it: nCLK, not_1_out, switchdt_1_p3
  _74161 _74161_1 (
    .pin1(nRESET), .pin2(switchdt_1_p3), .pin3(1'b0), .pin4(1'b0), .pin5(1'b0), .pin6(1'b0), .pin7(1'b1),
    .pin8(1'b0), .pin9(nDONE), .pin10(1'b1), .pin11(DVAL[3]), .pin12(DVAL[2]), .pin13(DVAL[1]),
    .pin14(DVAL[0]), .pin15(_74161_1_pin15), .pin16(1'b1));
  _74161 _74161_2 (
    .pin1(nRESET), .pin2(switchdt_1_p3), .pin3(1'b0), .pin4(1'b0), .pin5(1'b0), .pin6(1'b0), .pin7(1'b1),
    .pin8(1'b0), .pin9(nDONE), .pin10(_74161_1_pin15), .pin11(DVAL[7]), .pin12(DVAL[6]), .pin13(DVAL[5]),
    .pin14(DVAL[4]), .pin16(1'b1));  // open: pin15
  and and_1 (and_1_out, DVAL[0], DVAL[1], DVAL[2]);
  and and_2 (and_2_out, and_1_out, DVAL[3], DVAL[4]);
  Multiplexer #(.Selector_Bits(2)) multiplexer_1 (
    .sel(LEN), .in_0(1'b1), .in_1(and_1_out), .in_2(and_2_out), .in_3(DVAL[0]), .out(LAST));
  D_FF_AS d_ff_as_1 (.Set(~1'b1), .D(LAST), .C(CLK), .Clr(~nRESET), .Q(DONE), .nQ(nDONE));

  // Other names for the same wires on the sheet: Q0 = DVAL[0]; Q1 = DVAL[1]; Q2 = DVAL[2]; Q3 = DVAL[3]; Q4 = DVAL[4];
  //   Q5 = DVAL[5]; Q6 = DVAL[6]; Q7 = DVAL[7]

  // Notes on the sheet:
  //   CLK: Hz: 2
endmodule

/* Test case:
CLK  ~CLK ~RESET LEN  ~LAST ~DONE DVAL
0    1    0      0    0     0     X
0    1    1      0    0     0     X
1    0    1      0    0     0     X

0    1    1      0    0     0     X
1    0    1      0    0     0     X

0    1    1      1    1     0     X
1    0    1      1    1     1     X

loop (i,6)
0    1    1      1    1     1     X
1    0    1      1    1     1     X
end loop

0    1    1      1    0     1     X
1    0    1      1    0     0     X

0    1    1      2    1     0     X
1    0    1      2    1     1     X

loop (i,30)
0    1    1      2    1     1     X
1    0    1      2    1     1     X
end loop

0    1    1      0    0     1     X
1    0    1      0    0     0     X

0    1    1      3    1     0     X
1    0    1      3    1     1     X

0    1    1      3    0     1     X
1    0    1      3    0     0     X
*/
